// Logisim project Addresser.circ as structural Verilog: 2 circuits, main circuit M Addresser 16bits
// MEM
module M_Addresser_16bits (
  input  _7,
  input  _6,
  input  _5,
  input  _4,
  input  _3,
  input  _2,
  input  _1,
  input  _0,
  input  S,
  input  CL,
  input  CH,
  input  R,
  input  PCH_BUS,
  input  PCL_BUS,
  output _31,
  output _30,
  output _29,
  output _28,
  output _27,
  output _26,
  output _25,
  output _24,
  output _15,
  output _14,
  output _13,
  output _12,
  output _11,
  output _10,
  output _9,
  output _8,
  output _23,
  output _22,
  output _21,
  output _20,
  output _19,
  output _18,
  output _17,
  output _16
);

  wire and_1_out, and_2_out, inc_16bits_1__16, inc_16bits_1__17, inc_16bits_1__18, inc_16bits_1__19,
       inc_16bits_1__20, inc_16bits_1__21, inc_16bits_1__22, inc_16bits_1__23, inc_16bits_1__24,
       inc_16bits_1__25, inc_16bits_1__26, inc_16bits_1__27, inc_16bits_1__28, inc_16bits_1__29,
       inc_16bits_1__30, inc_16bits_1__31, not_1_out, not_2_out, not_3_out, tri_state_8bits_1__8,
       tri_state_8bits_1__9, tri_state_8bits_1__10, tri_state_8bits_1__11, tri_state_8bits_1__12,
       tri_state_8bits_1__13, tri_state_8bits_1__14, tri_state_8bits_1__15, tri_state_8bits_4__8,
       tri_state_8bits_4__9, tri_state_8bits_4__10, tri_state_8bits_4__11, tri_state_8bits_4__12,
       tri_state_8bits_4__13, tri_state_8bits_4__14, tri_state_8bits_4__15;

  not not_1 (not_1_out, PCL_BUS);
  Tri_State_8bits tri_state_8bits_1 (
    ._7(inc_16bits_1__31), ._6(inc_16bits_1__30), ._5(inc_16bits_1__29), ._4(inc_16bits_1__28),
    ._3(inc_16bits_1__27), ._2(inc_16bits_1__26), ._1(inc_16bits_1__25), ._0(inc_16bits_1__24),
    .E(not_2_out), ._15(tri_state_8bits_1__15), ._14(tri_state_8bits_1__14), ._13(tri_state_8bits_1__13),
    ._12(tri_state_8bits_1__12), ._11(tri_state_8bits_1__11), ._10(tri_state_8bits_1__10),
    ._9(tri_state_8bits_1__9), ._8(tri_state_8bits_1__8));
  not not_2 (not_2_out, S);
  Tri_State_8bits tri_state_8bits_2 (
    ._7(_23), ._6(_22), ._5(_21), ._4(_20), ._3(_19), ._2(_18), ._1(_17), ._0(_16), .E(and_1_out), ._15(_31),
    ._14(_30), ._13(_29), ._12(_28), ._11(_27), ._10(_26), ._9(_25), ._8(_24));
  and and_1 (and_1_out, PCH_BUS, not_1_out);
  Tri_State_8bits tri_state_8bits_3 (
    ._7(_7), ._6(_6), ._5(_5), ._4(_4), ._3(_3), ._2(_2), ._1(_1), ._0(_0), .E(S),
    ._15(tri_state_8bits_1__15), ._14(tri_state_8bits_1__14), ._13(tri_state_8bits_1__13),
    ._12(tri_state_8bits_1__12), ._11(tri_state_8bits_1__11), ._10(tri_state_8bits_1__10),
    ._9(tri_state_8bits_1__9), ._8(tri_state_8bits_1__8));
  Registrador_8_bits_S_Gatilho H (
    .R(R), .C(CH), ._7(tri_state_8bits_1__15), ._6(tri_state_8bits_1__14), ._5(tri_state_8bits_1__13),
    ._4(tri_state_8bits_1__12), ._3(tri_state_8bits_1__11), ._2(tri_state_8bits_1__10),
    ._1(tri_state_8bits_1__9), ._0(tri_state_8bits_1__8), ._15(_23), ._14(_22), ._13(_21), ._12(_20),
    ._11(_19), ._10(_18), ._9(_17), ._8(_16));
  Tri_State_8bits tri_state_8bits_4 (
    ._7(inc_16bits_1__23), ._6(inc_16bits_1__22), ._5(inc_16bits_1__21), ._4(inc_16bits_1__20),
    ._3(inc_16bits_1__19), ._2(inc_16bits_1__18), ._1(inc_16bits_1__17), ._0(inc_16bits_1__16),
    .E(not_2_out), ._15(tri_state_8bits_4__15), ._14(tri_state_8bits_4__14), ._13(tri_state_8bits_4__13),
    ._12(tri_state_8bits_4__12), ._11(tri_state_8bits_4__11), ._10(tri_state_8bits_4__10),
    ._9(tri_state_8bits_4__9), ._8(tri_state_8bits_4__8));
  Tri_State_8bits tri_state_8bits_5 (
    ._7(_7), ._6(_6), ._5(_5), ._4(_4), ._3(_3), ._2(_2), ._1(_1), ._0(_0), .E(S),
    ._15(tri_state_8bits_4__15), ._14(tri_state_8bits_4__14), ._13(tri_state_8bits_4__13),
    ._12(tri_state_8bits_4__12), ._11(tri_state_8bits_4__11), ._10(tri_state_8bits_4__10),
    ._9(tri_state_8bits_4__9), ._8(tri_state_8bits_4__8));
  Registrador_8_bits_S_Gatilho L (
    .R(R), .C(CL), ._7(tri_state_8bits_4__15), ._6(tri_state_8bits_4__14), ._5(tri_state_8bits_4__13),
    ._4(tri_state_8bits_4__12), ._3(tri_state_8bits_4__11), ._2(tri_state_8bits_4__10),
    ._1(tri_state_8bits_4__9), ._0(tri_state_8bits_4__8), ._15(_15), ._14(_14), ._13(_13), ._12(_12),
    ._11(_11), ._10(_10), ._9(_9), ._8(_8));
  Inc_16bits inc_16bits_1 (
    ._15(_23), ._14(_22), ._13(_21), ._12(_20), ._11(_19), ._10(_18), ._9(_17), ._8(_16), ._7(_15), ._6(_14),
    ._5(_13), ._4(_12), ._3(_11), ._2(_10), ._1(_9), ._0(_8), ._31(inc_16bits_1__31), ._30(inc_16bits_1__30),
    ._29(inc_16bits_1__29), ._28(inc_16bits_1__28), ._27(inc_16bits_1__27), ._26(inc_16bits_1__26),
    ._25(inc_16bits_1__25), ._24(inc_16bits_1__24), ._23(inc_16bits_1__23), ._22(inc_16bits_1__22),
    ._21(inc_16bits_1__21), ._20(inc_16bits_1__20), ._19(inc_16bits_1__19), ._18(inc_16bits_1__18),
    ._17(inc_16bits_1__17), ._16(inc_16bits_1__16));  // open: C
  Tri_State_8bits tri_state_8bits_6 (
    ._7(_15), ._6(_14), ._5(_13), ._4(_12), ._3(_11), ._2(_10), ._1(_9), ._0(_8), .E(and_2_out), ._15(_31),
    ._14(_30), ._13(_29), ._12(_28), ._11(_27), ._10(_26), ._9(_25), ._8(_24));
  and and_2 (and_2_out, PCL_BUS, not_3_out);
  not not_3 (not_3_out, PCH_BUS);

  // Notes on the sheet:
  //   Jean Jung
  //   Modulo de Endereçamento de Memória 16 Bits
  //   Seleção
  //   Clock L
  //   Clock H
  //   Reset
  //   16.. Output  ..8
  //   7.. Input  ..0
  //   7.. PC Bus  ..0
  //   7.. Output  ..0
endmodule

// Controller
module Control_Module (
  input  _7,
  input  _6,
  input  _5,
  input  _4,
  input  _3,
  input  _2,
  input  _1,
  input  _0,
  input  R,
  input  Clock,
  input  Flag_Z,
  input  Flag_C,
  output US0,
  output US1,
  output US2,
  output PBS0,
  output PBS1,
  output \Fim_de_Instrução ,
  output Sel_SP,
  output ULA_Bus,
  output BUF_Clock,
  output AC_Bus,
  output AC_Clock,
  output Reg_Bus,
  output Reg_Clock,
  output RAM_rd,
  output RAM_wr,
  output RAM_cs,
  output IN_bus,
  output OUT_clock,
  output ROM_rd,
  output ROM_cs,
  output PCH_bus,
  output PCL_bus,
  output PCH_Clock,
  output SelDataPC,
  output DIRClock,
  output SPIncDec,
  output PCL_Clock,
  output SP_Clock,
  output SP_Enable
);

  wire and_6_out, and_7_out, counter_5bits_1__0, counter_5bits_1__1, counter_5bits_1__2, counter_5bits_1__3,
       counter_5bits_1__4, inc_8bits_1__8, inc_8bits_1__9, inc_8bits_1__10, inc_8bits_1__11, inc_8bits_1__12,
       inc_8bits_1__13, inc_8bits_1__14, inc_8bits_1__15, nor_2_out, not_1_out, or_1_out, or_2_out,
       tri_state_8bits_1__8, tri_state_8bits_1__9, tri_state_8bits_1__10, tri_state_8bits_1__11,
       tri_state_8bits_1__12, tri_state_8bits_1__13, tri_state_8bits_1__14, tri_state_8bits_1__15;
  wire [7:0] JC__8, RI__8, rom_1_data;
  wire [11:0] rom_3_data;
  wire [15:12] rom_2_data;

  nor nor_1 (\Fim_de_Instrução , JC__8[0], JC__8[1], JC__8[2], JC__8[3], JC__8[4], JC__8[5], JC__8[6], JC__8[7]);
  Registrador_8_bits_S_Gatilho RI (
    .C(rom_3_data[3]), ._7(_7), ._6(_6), ._5(_5), ._4(_4), ._3(_3), ._2(_2), ._1(_1), ._0(_0), ._15(US2),
    ._14(US1), ._13(US0), ._12(PBS1), ._11(PBS0), ._10(RI__8[2]), ._9(RI__8[1]), ._8(RI__8[0]));  // open: R
  Inc_8bits inc_8bits_1 (
    ._7(JC__8[7]), ._6(JC__8[6]), ._5(JC__8[5]), ._4(JC__8[4]), ._3(JC__8[3]), ._2(JC__8[2]), ._1(JC__8[1]),
    ._0(JC__8[0]), ._15(inc_8bits_1__15), ._14(inc_8bits_1__14), ._13(inc_8bits_1__13),
    ._12(inc_8bits_1__12), ._11(inc_8bits_1__11), ._10(inc_8bits_1__10), ._9(inc_8bits_1__9),
    ._8(inc_8bits_1__8));  // open: C
  Tri_State_8bits tri_state_8bits_1 (
    ._7(inc_8bits_1__15), ._6(inc_8bits_1__14), ._5(inc_8bits_1__13), ._4(inc_8bits_1__12),
    ._3(inc_8bits_1__11), ._2(inc_8bits_1__10), ._1(inc_8bits_1__9), ._0(inc_8bits_1__8), .E(not_1_out),
    ._15(tri_state_8bits_1__15), ._14(tri_state_8bits_1__14), ._13(tri_state_8bits_1__13),
    ._12(tri_state_8bits_1__12), ._11(tri_state_8bits_1__11), ._10(tri_state_8bits_1__10),
    ._9(tri_state_8bits_1__9), ._8(tri_state_8bits_1__8));
  not not_1 (not_1_out, rom_3_data[4]);
  and and_1 (RI__8[3], rom_2_data[12], counter_5bits_1__0);
  Counter_5bits counter_5bits_1 (
    .enable(rom_2_data[12]), .reset(rom_2_data[13]), .clock(rom_3_data[5]), .Inc_Dec(1'b0),
    ._0(counter_5bits_1__0), ._1(counter_5bits_1__1), ._2(counter_5bits_1__2), ._3(counter_5bits_1__3),
    ._4(counter_5bits_1__4));
  and and_2 (RI__8[6], rom_2_data[12], counter_5bits_1__3);
  and and_3 (RI__8[4], rom_2_data[12], counter_5bits_1__1);
  and and_4 (RI__8[5], rom_2_data[12], counter_5bits_1__2);
  and and_5 (RI__8[7], rom_2_data[12], counter_5bits_1__4);
  Tri_State_8bits tri_state_8bits_2 (
    ._7(rom_1_data[7]), ._6(rom_1_data[6]), ._5(rom_1_data[5]), ._4(rom_1_data[4]), ._3(rom_1_data[3]),
    ._2(rom_1_data[2]), ._1(rom_1_data[1]), ._0(rom_1_data[0]), .E(rom_3_data[4]),
    ._15(tri_state_8bits_1__15), ._14(tri_state_8bits_1__14), ._13(tri_state_8bits_1__13),
    ._12(tri_state_8bits_1__12), ._11(tri_state_8bits_1__11), ._10(tri_state_8bits_1__10),
    ._9(tri_state_8bits_1__9), ._8(tri_state_8bits_1__8));
  ROM rom_1 (.addr(RI__8), .data(rom_1_data));  // open: sel
  Registrador_8_bits_S_Gatilho JC (
    .R(or_1_out), .C(Clock), ._7(tri_state_8bits_1__15), ._6(tri_state_8bits_1__14),
    ._5(tri_state_8bits_1__13), ._4(tri_state_8bits_1__12), ._3(tri_state_8bits_1__11),
    ._2(tri_state_8bits_1__10), ._1(tri_state_8bits_1__9), ._0(tri_state_8bits_1__8), ._15(JC__8[7]),
    ._14(JC__8[6]), ._13(JC__8[5]), ._12(JC__8[4]), ._11(JC__8[3]), ._10(JC__8[2]), ._9(JC__8[1]),
    ._8(JC__8[0]));
  ROM #(.dataWidth(16)) rom_2 (
    .addr(JC__8),
    .data({rom_2_data, OUT_clock, IN_bus, RAM_cs, RAM_wr, RAM_rd, Reg_Clock, Reg_Bus, AC_Clock, AC_Bus, BUF_Clock, ULA_Bus, Sel_SP}));  // open: sel
  ROM #(.dataWidth(16)) rom_3 (
    .addr(JC__8),
    .data({SPIncDec, SP_Clock, DIRClock, SelDataPC, rom_3_data[11:10], PCL_bus, PCH_bus, ROM_cs, ROM_rd, rom_3_data[5:0]}));  // open: sel
  or or_1 (or_1_out, R, rom_3_data[0]);
  nor nor_2 (nor_2_out, rom_3_data[2], rom_3_data[1]);
  and and_6 (and_6_out, rom_3_data[1], Flag_C);
  and and_7 (and_7_out, rom_3_data[2], Flag_Z);
  and and_8 (PCH_Clock, rom_3_data[10], or_2_out);
  or or_2 (or_2_out, nor_2_out, and_6_out, and_7_out);
  and and_9 (PCL_Clock, or_2_out, rom_3_data[11]);

  assign SP_Enable = SP_Clock;

  // Notes on the sheet:
  //   Jean Jung
  //   Módulo de Controle
  //   ULA
  //   PortBank
  //   7.. Input  ..0
  //   Decodificador de Instrução
  //   contents of rom_1 (hex, n*v repeats v):
  //   3 8 d 14 19 1e 25 2a 2c 31 36 3d 49 56 63 2a 7f 84 8b 91 94 98 9b 2a 7*0 2a 7*0 2a 7*0 2a 7*0 2a 7*0
  //   2a 7*0 2a 7*0 2a 7*0 2a 7*0 2a 7*0 2a 7*0 2a 7*0 2a 7*0 2a 7*0 2a 7*0 2a 7*0 2a 7*0 2a 7*0 2a 7*0 2a
  //   7*0 2a 7*0 2a 7*0 2a 7*0 2a 7*0 2a 7*0 2a 7*0 2a 7*0 2a 7*0 2a 7*0 2a
  //   Controle B
  //   Controle A
  //   contents of rom_2 (hex, n*v repeats v):
  //   2000 0 0 8 4 2 10 0 8 4 2 40 0 0 0 8 4 2 302 0 808 c 2 800 0 20 4 2 10 0 0 0 280 4 2 10 0 400 4 2 10
  //   0 0 1000 0 4 2 10 0 0 4 2 40 0 0 4 0 0 2 302 0 0 1 301 0 0 1 301 281 0 281 0 0 0 1 301 0 0 1 301 0
  //   281 0 281 0 0 0 1 301 0 0 1 301 0 281 0 281 6*0 1 301 0 0 1 301 5*0 1 301 1 301 4*0 281 0 281 0 0
  //   281 0 281 0 0 20 20 280 4 2 10 0 20 20 8 4 2 302 0 20 321 281 2c1 0 0 0 8 309 281 291
  //   HD
  //   HD Res
  //   CRes
  //   CResC
  //   CResZ
  //   RIClock
  //   SeIRI
  //   HD Clock
  //   contents of rom_3 (hex, n*v repeats v):
  //   0 c0 c18 4*0 1 4*0 1 c0 2c00 4*0 1 4*0 1 4*0 1 c0 2c00 4*0 1 4*0 1 e0 c18 c0 c00 0 0 1 c0 c00 0 0 1
  //   c0 c00 c0 2c00 0 0 1 8000 c0c0 80c0 c00 80c0 c0c0 c0 1000 4800 1000 4400 1 8000 c0c0 80c0 c00 80c0
  //   c0c0 c0 c00 1002 4802 1002 4402 1 8000 c0c0 80c0 c00 80c0 c0c0 c0 c00 1004 4804 1004 4404 1 8000
  //   c000 8000 c000 80c0 c0c0 c00 80c0 c0c0 c0 c00 4000 0 4000 0 4000 8100 c200 200 8000 c000 8000 c000
  //   1000 4800 1000 4400 1 1000 4800 1000 4400 1 0 2000 4*0 1 0 2000 0 0 0 1 8000 c000 1 0 0 4000 1 8000
  //   c000 1 0 0 4000 1
  //   Clock PCH
  //   Clock PCL
  //   SP Clock
endmodule
