// Logisim project Arithmetics.circ as structural Verilog: 11 circuits, main circuit SOMA 1bit 2op
// +
module SOMA_1bit_2op (
  input  A,
  input  B,
  input  C_1,
  output S,
  output C
);

  wire and_1_out, and_2_out, or_1_out, xor_1_out;

  or or_1 (or_1_out, A, B);
  xor xor_1 (xor_1_out, A, B);
  xor xor_2 (S, xor_1_out, C_1);
  and and_1 (and_1_out, A, B);
  and and_2 (and_2_out, or_1_out, C_1);
  or or_2 (C, and_1_out, and_2_out);

  // Notes on the sheet:
  //   SOMA 1bit 2op
  //   Jean Jung
  //   Operandos
  //   Carrier
endmodule

// +\- 8bits
module SOMA_SUB_8bits (
  input  _7,
  input  _6,
  input  _5,
  input  _4,
  input  _3,
  input  _2,
  input  _1,
  input  _0,
  input  _15,
  input  _14,
  input  _13,
  input  _12,
  input  _11,
  input  _10,
  input  _9,
  input  _8,
  input  O,
  output Cn_1,
  output _23,
  output _22,
  output _21,
  output _20,
  output _19,
  output _18,
  output _17,
  output _16
);

  wire soma_1bit_2op_1_c, soma_1bit_2op_2_c, soma_1bit_2op_3_c, soma_1bit_2op_4_c, soma_1bit_2op_5_c,
       soma_1bit_2op_6_c, soma_1bit_2op_7_c, soma_1bit_2op_8_c, xor_8bits_2op_1__16, xor_8bits_2op_1__17,
       xor_8bits_2op_1__18, xor_8bits_2op_1__19, xor_8bits_2op_1__20, xor_8bits_2op_1__21,
       xor_8bits_2op_1__22, xor_8bits_2op_1__23;

  xor xor_1 (Cn_1, soma_1bit_2op_1_c, O);
  SOMA_1bit_2op soma_1bit_2op_1 (
    .A(_7), .B(xor_8bits_2op_1__23), .C_1(soma_1bit_2op_2_c), .S(_23), .C(soma_1bit_2op_1_c));
  SOMA_1bit_2op soma_1bit_2op_2 (
    .A(_6), .B(xor_8bits_2op_1__22), .C_1(soma_1bit_2op_3_c), .S(_22), .C(soma_1bit_2op_2_c));
  SOMA_1bit_2op soma_1bit_2op_3 (
    .A(_5), .B(xor_8bits_2op_1__21), .C_1(soma_1bit_2op_4_c), .S(_21), .C(soma_1bit_2op_3_c));
  SOMA_1bit_2op soma_1bit_2op_4 (
    .A(_4), .B(xor_8bits_2op_1__20), .C_1(soma_1bit_2op_5_c), .S(_20), .C(soma_1bit_2op_4_c));
  SOMA_1bit_2op soma_1bit_2op_5 (
    .A(_3), .B(xor_8bits_2op_1__19), .C_1(soma_1bit_2op_7_c), .S(_19), .C(soma_1bit_2op_5_c));
  SOMA_1bit_2op soma_1bit_2op_6 (
    .A(_1), .B(xor_8bits_2op_1__17), .C_1(soma_1bit_2op_8_c), .S(_17), .C(soma_1bit_2op_6_c));
  SOMA_1bit_2op soma_1bit_2op_7 (
    .A(_2), .B(xor_8bits_2op_1__18), .C_1(soma_1bit_2op_6_c), .S(_18), .C(soma_1bit_2op_7_c));
  SOMA_1bit_2op soma_1bit_2op_8 (.A(_0), .B(xor_8bits_2op_1__16), .C_1(O), .S(_16), .C(soma_1bit_2op_8_c));
  Xor_8bits_2op xor_8bits_2op_1 (
    ._7(_15), ._15(O), ._6(_14), ._14(O), ._5(_13), ._13(O), ._4(_12), ._12(O), ._3(_11), ._11(O), ._2(_10),
    ._10(O), ._1(_9), ._9(O), ._0(_8), ._8(O), ._23(xor_8bits_2op_1__23), ._22(xor_8bits_2op_1__22),
    ._21(xor_8bits_2op_1__21), ._20(xor_8bits_2op_1__20), ._19(xor_8bits_2op_1__19),
    ._18(xor_8bits_2op_1__18), ._17(xor_8bits_2op_1__17), ._16(xor_8bits_2op_1__16));

  // Notes on the sheet:
  //   Jean Jung
  //   Somador subtrador 8bits
  //   7.. Output  ..0
  //   7.. Input A  ..0
  //   7.. Input B  ..0
  //   Operação (+-)
endmodule

// +1
module Inc_1Bit (
  input  A,
  input  C_1,
  output S,
  output C
);

  xor xor_1 (S, A, C_1);
  and and_1 (C, A, C_1);

  // Notes on the sheet:
  //   Inc 1bit
  //   Jean Jung
  //   Operandos
  //   Carrier
endmodule

module Inc_8bits (
  input  _7,
  input  _6,
  input  _5,
  input  _4,
  input  _3,
  input  _2,
  input  _1,
  input  _0,
  output C,
  output _15,
  output _14,
  output _13,
  output _12,
  output _11,
  output _10,
  output _9,
  output _8
);

  wire inc_1bit_2_c, inc_1bit_3_c, inc_1bit_4_c, inc_1bit_5_c, inc_1bit_6_c, inc_1bit_7_c, inc_1bit_8_c;

  Inc_1Bit inc_1bit_1 (.A(_7), .C_1(inc_1bit_2_c), .S(_15), .C(C));
  Inc_1Bit inc_1bit_2 (.A(_6), .C_1(inc_1bit_3_c), .S(_14), .C(inc_1bit_2_c));
  Inc_1Bit inc_1bit_3 (.A(_5), .C_1(inc_1bit_4_c), .S(_13), .C(inc_1bit_3_c));
  Inc_1Bit inc_1bit_4 (.A(_4), .C_1(inc_1bit_5_c), .S(_12), .C(inc_1bit_4_c));
  Inc_1Bit inc_1bit_5 (.A(_3), .C_1(inc_1bit_7_c), .S(_11), .C(inc_1bit_5_c));
  Inc_1Bit inc_1bit_6 (.A(_1), .C_1(inc_1bit_8_c), .S(_9), .C(inc_1bit_6_c));
  Inc_1Bit inc_1bit_7 (.A(_2), .C_1(inc_1bit_6_c), .S(_10), .C(inc_1bit_7_c));
  Inc_1Bit inc_1bit_8 (.A(_0), .C_1(1'b1), .S(_8), .C(inc_1bit_8_c));

  // Notes on the sheet:
  //   Inc 8bits
  //   Jean Jung
  //   7.. Output  ..0
  //   7.. Input A  ..0
endmodule

module Inc_16bits (
  input  _15,
  input  _14,
  input  _13,
  input  _12,
  input  _11,
  input  _10,
  input  _9,
  input  _8,
  input  _7,
  input  _6,
  input  _5,
  input  _4,
  input  _3,
  input  _2,
  input  _1,
  input  _0,
  output C,
  output _31,
  output _30,
  output _29,
  output _28,
  output _27,
  output _26,
  output _25,
  output _24,
  output _23,
  output _22,
  output _21,
  output _20,
  output _19,
  output _18,
  output _17,
  output _16
);

  wire inc_8bits_1_c;

  Inc_8bits_c__Carrier inc_8bits_c_carrier_1 (
    .C(C), .C_1(inc_8bits_1_c), ._7(_15), ._6(_14), ._5(_13), ._4(_12), ._3(_11), ._2(_10), ._1(_9), ._0(_8),
    ._15(_31), ._14(_30), ._13(_29), ._12(_28), ._11(_27), ._10(_26), ._9(_25), ._8(_24));
  Inc_8bits inc_8bits_1 (
    .C(inc_8bits_1_c), ._7(_7), ._6(_6), ._5(_5), ._4(_4), ._3(_3), ._2(_2), ._1(_1), ._0(_0), ._15(_23),
    ._14(_22), ._13(_21), ._12(_20), ._11(_19), ._10(_18), ._9(_17), ._8(_16));

  // Notes on the sheet:
  //   Jean Jung
  //   Inc 16 Bits
  //   15.. Input B  ..8
  //   15.. Output  ..8
  //   7.. Input A  ..0
  //   7.. Output  ..0
endmodule

// Inc 8bits C-1
module Inc_8bits_c__Carrier (
  input  _7,
  input  _6,
  input  _5,
  input  _4,
  input  _3,
  input  _2,
  input  _1,
  input  _0,
  input  C_1,
  output C,
  output _15,
  output _14,
  output _13,
  output _12,
  output _11,
  output _10,
  output _9,
  output _8
);

  wire inc_1bit_2_c, inc_1bit_3_c, inc_1bit_4_c, inc_1bit_5_c, inc_1bit_6_c, inc_1bit_7_c, inc_1bit_8_c;

  Inc_1Bit inc_1bit_1 (.A(_7), .C_1(inc_1bit_2_c), .S(_15), .C(C));
  Inc_1Bit inc_1bit_2 (.A(_6), .C_1(inc_1bit_3_c), .S(_14), .C(inc_1bit_2_c));
  Inc_1Bit inc_1bit_3 (.A(_5), .C_1(inc_1bit_4_c), .S(_13), .C(inc_1bit_3_c));
  Inc_1Bit inc_1bit_4 (.A(_4), .C_1(inc_1bit_5_c), .S(_12), .C(inc_1bit_4_c));
  Inc_1Bit inc_1bit_5 (.A(_3), .C_1(inc_1bit_7_c), .S(_11), .C(inc_1bit_5_c));
  Inc_1Bit inc_1bit_6 (.A(_1), .C_1(inc_1bit_8_c), .S(_9), .C(inc_1bit_6_c));
  Inc_1Bit inc_1bit_7 (.A(_2), .C_1(inc_1bit_6_c), .S(_10), .C(inc_1bit_7_c));
  Inc_1Bit inc_1bit_8 (.A(_0), .C_1(C_1), .S(_8), .C(inc_1bit_8_c));

  // Notes on the sheet:
  //   Jean Jung
  //   Inc 8bits c\Carrier
  //   7.. Output  ..0
  //   7.. Input A  ..0
endmodule

// Cnt
module Counter (
  input  clock,
  input  enable,
  input  reset,
  input  Inc_Dec,
  output S,
  output C___1
);

  wire and_1_out, and_2_out, j_k_ff_1_qn, not_1_out;

  J_K_Flip_Flop #(.trigger("falling")) j_k_ff_1 (
    .J(1'b1), .clk(clock), .K(1'b1), .Q(S), .Qn(j_k_ff_1_qn), .en(enable), .reset(reset));  // open: preset
  not not_1 (not_1_out, Inc_Dec);
  and and_1 (and_1_out, S, enable, not_1_out);
  or or_1 (C___1, and_1_out, and_2_out);
  and and_2 (and_2_out, j_k_ff_1_qn, enable, Inc_Dec);

  // Notes on the sheet:
  //   Contador Binário
  //   Jean Jung
endmodule

// Count
module Counter_8bits (
  input  enable,
  input  reset,
  input  clock,
  input  Inc_Dec,
  output _0,
  output _1,
  output _2,
  output _3,
  output _4,
  output _5,
  output _6,
  output _7
);

  wire counter_1_c___1, counter_2_c___1, counter_3_c___1, counter_4_c___1, counter_5_c___1, counter_6_c___1,
       counter_7_c___1;

  Counter counter_1 (.clock(clock), .reset(reset), .Inc_Dec(Inc_Dec), .S(_0), .C___1(counter_1_c___1), .enable(enable));
  Counter counter_2 (
    .clock(counter_1_c___1), .reset(reset), .Inc_Dec(Inc_Dec), .S(_1), .C___1(counter_2_c___1),
    .enable(enable));
  Counter counter_3 (
    .clock(counter_2_c___1), .reset(reset), .Inc_Dec(Inc_Dec), .S(_2), .C___1(counter_3_c___1),
    .enable(enable));
  Counter counter_4 (
    .clock(counter_3_c___1), .reset(reset), .Inc_Dec(Inc_Dec), .S(_3), .C___1(counter_4_c___1),
    .enable(enable));
  Counter counter_5 (
    .clock(counter_4_c___1), .reset(reset), .Inc_Dec(Inc_Dec), .S(_4), .C___1(counter_5_c___1),
    .enable(enable));
  Counter counter_6 (
    .clock(counter_5_c___1), .reset(reset), .Inc_Dec(Inc_Dec), .S(_5), .C___1(counter_6_c___1),
    .enable(enable));
  Counter counter_7 (
    .clock(counter_6_c___1), .reset(reset), .Inc_Dec(Inc_Dec), .S(_6), .C___1(counter_7_c___1),
    .enable(enable));
  Counter counter_8 (
    .clock(counter_7_c___1), .reset(reset), .Inc_Dec(Inc_Dec), .S(_7), .enable(enable));  // open: C___1

  // Notes on the sheet:
  //   Counter 8bits
  //   Jean Jung
  //   7.. Output  ..0
endmodule

// Count
module Counter_______8bits (
  input  in_1,
  input  reset,
  input  clock,
  input  enable,
  output _0,
  output _1,
  output _2,
  output _3,
  output _4,
  output _5,
  output _6,
  output _7
);

  wire registrador_8bits_c_buffer_1__16, registrador_8bits_c_buffer_1__17, registrador_8bits_c_buffer_1__18,
       registrador_8bits_c_buffer_1__19, registrador_8bits_c_buffer_1__20, registrador_8bits_c_buffer_1__21,
       registrador_8bits_c_buffer_1__22, registrador_8bits_c_buffer_1__23, soma_sub_8bits_1__16,
       soma_sub_8bits_1__17, soma_sub_8bits_1__18, soma_sub_8bits_1__19, soma_sub_8bits_1__20,
       soma_sub_8bits_1__21, soma_sub_8bits_1__22, soma_sub_8bits_1__23;

  SOMA_SUB_8bits soma_sub_8bits_1 (
    .O(in_1), ._7(registrador_8bits_c_buffer_1__23), ._6(registrador_8bits_c_buffer_1__22),
    ._5(registrador_8bits_c_buffer_1__21), ._4(registrador_8bits_c_buffer_1__20),
    ._3(registrador_8bits_c_buffer_1__19), ._2(registrador_8bits_c_buffer_1__18),
    ._1(registrador_8bits_c_buffer_1__17), ._0(registrador_8bits_c_buffer_1__16), ._15(1'b0), ._14(1'b0),
    ._13(1'b0), ._12(1'b0), ._11(1'b0), ._10(1'b0), ._9(1'b0), ._8(1'b1), ._23(soma_sub_8bits_1__23),
    ._22(soma_sub_8bits_1__22), ._21(soma_sub_8bits_1__21), ._20(soma_sub_8bits_1__20),
    ._19(soma_sub_8bits_1__19), ._18(soma_sub_8bits_1__18), ._17(soma_sub_8bits_1__17),
    ._16(soma_sub_8bits_1__16));  // open: Cn_1
  Registrador_8bits_c__buffer registrador_8bits_c_buffer_1 (
    .E(enable), .R(reset), .C(clock), ._7(soma_sub_8bits_1__23), ._6(soma_sub_8bits_1__22),
    ._5(soma_sub_8bits_1__21), ._4(soma_sub_8bits_1__20), ._3(soma_sub_8bits_1__19),
    ._2(soma_sub_8bits_1__18), ._1(soma_sub_8bits_1__17), ._0(soma_sub_8bits_1__16),
    ._23(registrador_8bits_c_buffer_1__23), ._22(registrador_8bits_c_buffer_1__22),
    ._21(registrador_8bits_c_buffer_1__21), ._20(registrador_8bits_c_buffer_1__20),
    ._19(registrador_8bits_c_buffer_1__19), ._18(registrador_8bits_c_buffer_1__18),
    ._17(registrador_8bits_c_buffer_1__17), ._16(registrador_8bits_c_buffer_1__16), ._15(_7), ._14(_6),
    ._13(_5), ._12(_4), ._11(_3), ._10(_2), ._9(_1), ._8(_0));

  // Notes on the sheet:
  //   Jean Jung
  //   0.. Outputs ..7
  //   Contador de Incremento\Decremento
endmodule

// Counter
module Counter_4bits (
  input  enable,
  input  reset,
  input  clock,
  input  Inc_Dec,
  output _0,
  output _1,
  output _2,
  output _3
);

  wire counter_1_c___1, counter_2_c___1, counter_3_c___1;

  Counter counter_1 (.clock(clock), .reset(reset), .Inc_Dec(Inc_Dec), .S(_0), .C___1(counter_1_c___1), .enable(enable));
  Counter counter_2 (
    .clock(counter_1_c___1), .reset(reset), .Inc_Dec(Inc_Dec), .S(_1), .C___1(counter_2_c___1),
    .enable(enable));
  Counter counter_3 (
    .clock(counter_2_c___1), .reset(reset), .Inc_Dec(Inc_Dec), .S(_2), .C___1(counter_3_c___1),
    .enable(enable));
  Counter counter_4 (
    .clock(counter_3_c___1), .reset(reset), .Inc_Dec(Inc_Dec), .S(_3), .enable(enable));  // open: C___1

  // Notes on the sheet:
  //   Counter 4bits
  //   Jean Jung
  //   0.. Output  ..4
endmodule

// Counter
module Counter_5bits (
  input  enable,
  input  reset,
  input  clock,
  input  Inc_Dec,
  output _0,
  output _1,
  output _2,
  output _3,
  output _4
);

  wire counter_1_c___1, counter_2_c___1, counter_3_c___1, counter_4_c___1;

  Counter counter_1 (
    .clock(counter_2_c___1), .reset(reset), .Inc_Dec(Inc_Dec), .S(_1), .C___1(counter_1_c___1),
    .enable(enable));
  Counter counter_2 (.clock(clock), .reset(reset), .Inc_Dec(Inc_Dec), .S(_0), .C___1(counter_2_c___1), .enable(enable));
  Counter counter_3 (
    .clock(counter_1_c___1), .reset(reset), .Inc_Dec(Inc_Dec), .S(_2), .C___1(counter_3_c___1),
    .enable(enable));
  Counter counter_4 (
    .clock(counter_3_c___1), .reset(reset), .Inc_Dec(Inc_Dec), .S(_3), .C___1(counter_4_c___1),
    .enable(enable));
  Counter counter_5 (
    .clock(counter_4_c___1), .reset(reset), .Inc_Dec(Inc_Dec), .S(_4), .enable(enable));  // open: C___1

  // Notes on the sheet:
  //   Counter 5bits
  //   Jean Jung
  //   0.. Output  ..4
endmodule
