// Logisim project Demux.circ as structural Verilog: 1 circuit, main circuit Demux4
// DMX4
module Demux4 (
  input  S2,
  input  S1,
  input  D,
  output out_4,
  output out_5,
  output out_6,
  output out_7
);

  wire nor_1_out, not_1_out, not_2_out;

  not not_1 (not_1_out, S1);
  not not_2 (not_2_out, S2);
  nor nor_1 (nor_1_out, S1, S2);
  and and_1 (out_4, S1, S2, D);
  and and_2 (out_5, not_1_out, S2, D);
  and and_3 (out_6, S1, not_2_out, D);
  and and_4 (out_7, nor_1_out, D);

  // Notes on the sheet:
  //   Demux 1 - 4
  //   Jean Jung
  //   Seleção
  //   Output
endmodule
