// Logisim project Logics.circ as structural Verilog: 4 circuits, main circuit Not 8bits
// NOT
module Not_8bits (
  input  _7,
  input  _6,
  input  _5,
  input  _4,
  input  _3,
  input  _2,
  input  _1,
  input  _0,
  output _15,
  output _14,
  output _13,
  output _12,
  output _11,
  output _10,
  output _9,
  output _8
);

  not not_1 (_14, _6);
  not not_2 (_15, _7);
  not not_3 (_12, _4);
  not not_4 (_11, _3);
  not not_5 (_10, _2);
  not not_6 (_13, _5);
  not not_7 (_9, _1);
  not not_8 (_8, _0);

  // Notes on the sheet:
  //   Jean Jung
  //   NOT 8 bits
  //   7.. Input  ..0
  //   7.. Output  ..0
endmodule

// XOR
module Xor_8bits_2op (
  input  _7,
  input  _6,
  input  _5,
  input  _4,
  input  _3,
  input  _2,
  input  _1,
  input  _0,
  input  _15,
  input  _14,
  input  _13,
  input  _12,
  input  _11,
  input  _10,
  input  _9,
  input  _8,
  output _23,
  output _22,
  output _21,
  output _20,
  output _19,
  output _18,
  output _17,
  output _16
);

  xor xor_1 (_23, _7, _15);
  xor xor_2 (_22, _6, _14);
  xor xor_3 (_21, _5, _13);
  xor xor_4 (_20, _4, _12);
  xor xor_5 (_19, _3, _11);
  xor xor_6 (_18, _2, _10);
  xor xor_7 (_17, _1, _9);
  xor xor_8 (_16, _0, _8);

  // Notes on the sheet:
  //   Jean Jung
  //   XOR 8bits 2op
  //   7.. Output  ..0
  //   7.. Input A  ..0
  //   7.. Input B  ..0
endmodule

// OR
module Or_8bits_2op (
  input  _7,
  input  _6,
  input  _5,
  input  _4,
  input  _3,
  input  _2,
  input  _1,
  input  _0,
  input  _15,
  input  _14,
  input  _13,
  input  _12,
  input  _11,
  input  _10,
  input  _9,
  input  _8,
  output _23,
  output _22,
  output _21,
  output _20,
  output _19,
  output _18,
  output _17,
  output _16
);

  or or_1 (_23, _7, _15);
  or or_2 (_21, _5, _13);
  or or_3 (_22, _6, _14);
  or or_4 (_19, _3, _11);
  or or_5 (_20, _4, _12);
  or or_6 (_18, _2, _10);
  or or_7 (_17, _1, _9);
  or or_8 (_16, _0, _8);

  // Notes on the sheet:
  //   Jean Jung
  //   OR 8bits 2op
  //   7.. Output  ..0
  //   7.. Input A  ..0
  //   7.. Input B  ..0
endmodule

// AND
module And_8bits_2op (
  input  _7,
  input  _6,
  input  _5,
  input  _4,
  input  _3,
  input  _2,
  input  _1,
  input  _0,
  input  _15,
  input  _14,
  input  _13,
  input  _12,
  input  _11,
  input  _10,
  input  _9,
  input  _8,
  output _23,
  output _22,
  output _21,
  output _20,
  output _19,
  output _18,
  output _17,
  output _16
);

  and and_1 (_23, _7, _15);
  and and_2 (_22, _6, _14);
  and and_3 (_21, _5, _13);
  and and_4 (_19, _3, _11);
  and and_5 (_20, _4, _12);
  and and_6 (_18, _2, _10);
  and and_7 (_16, _0, _8);
  and and_8 (_17, _1, _9);

  // Notes on the sheet:
  //   Jean Jung
  //   AND 8bits 2op
  //   7.. Output  ..0
  //   7.. Input A  ..0
  //   7.. Input B  ..0
endmodule
