// Logisim project M++.circ as structural Verilog: 1 circuit, main circuit M++
// M+++
module M (
  input  Reset,
  input  _23,
  input  _22,
  input  _21,
  input  _20,
  input  _19,
  input  _18,
  input  _17,
  input  _16,
  input  _31,
  input  _30,
  input  _29,
  input  _28,
  input  _27,
  input  _26,
  input  _25,
  input  _24,
  input  _47,
  input  _46,
  input  _45,
  input  _44,
  input  _43,
  input  _42,
  input  _41,
  input  _40,
  input  _63,
  input  _62,
  input  _61,
  input  _60,
  input  _59,
  input  _58,
  input  _57,
  input  _56,
  input  _79,
  input  _78,
  input  _77,
  input  _76,
  input  _75,
  input  _74,
  input  _73,
  input  _72,
  input  _105,
  output _103,
  output _102,
  output _101,
  output _100,
  output _99,
  output _98,
  output _97,
  output _96,
  output _104,
  output ROM_read,
  output ROM_cs,
  output _39,
  output _38,
  output _37,
  output _36,
  output _35,
  output _34,
  output _33,
  output _32,
  output _55,
  output _54,
  output _53,
  output _52,
  output _51,
  output _50,
  output _49,
  output _48,
  output _71,
  output _70,
  output _69,
  output _68,
  output _67,
  output _66,
  output _65,
  output _64,
  output _87,
  output _86,
  output _85,
  output _84,
  output _83,
  output _82,
  output _81,
  output _80,
  output _95,
  output _94,
  output _93,
  output _92,
  output _91,
  output _90,
  output _89,
  output _88,
  output _15,
  output _14,
  output _13,
  output _12,
  output _11,
  output _10,
  output _9,
  output _8,
  output _7,
  output _6,
  output _5,
  output _4,
  output _3,
  output _2,
  output _1,
  output _0,
  output RAM_read,
  output RAM_write,
  output RAM_cs
);

  wire Acumulador__16, Acumulador__17, Acumulador__18, Acumulador__19, Acumulador__20, Acumulador__21,
       Acumulador__22, Acumulador__23, and_1_out, and_3_out, Buffer__8, Buffer__9, Buffer__10, Buffer__11,
       Buffer__12, Buffer__13, Buffer__14, Buffer__15, clock_1_out, control_module_1_ac_bus,
       control_module_1_ac_clock, control_module_1_buf_clock, control_module_1_dirclock,
       control_module_1_in_bus, control_module_1_out_clock, control_module_1_pbs0, control_module_1_pbs1,
       control_module_1_pch_bus, control_module_1_pch_clock, control_module_1_pcl_bus,
       control_module_1_pcl_clock, control_module_1_ram_cs, control_module_1_reg_bus,
       control_module_1_reg_clock, control_module_1_sel_sp, control_module_1_seldatapc,
       control_module_1_sp_clock, control_module_1_spincdec, control_module_1_ula_bus, control_module_1_us0,
       control_module_1_us1, control_module_1_us2, DIR__8, DIR__9, DIR__10, DIR__11, DIR__12, DIR__13,
       DIR__14, DIR__15, not_1_out, not_2_out, not_3_out, or_1_out, or_2_out, SP__0, SP__1, SP__2, SP__3,
       SP__4, SP__5, SP__6, SP__7, ula_8bits_1_fc, ula_8bits_1_fz;
  wire [7:0] tri_state_8bits_2__8, tri_state_8bits_4__8;

  Clock clock_1 (.out(clock_1_out));
  and and_1 (and_1_out, clock_1_out, 1'b1, not_1_out);
  or or_1 (or_1_out, _105, and_1_out);
  not not_1 (not_1_out, _104);
  or or_2 (or_2_out, ROM_read, RAM_read);
  not not_2 (not_2_out, or_2_out);
  Tri_State_8bits tri_state_8bits_1 (
    ._7(tri_state_8bits_2__8[7]), ._6(tri_state_8bits_2__8[6]), ._5(tri_state_8bits_2__8[5]),
    ._4(tri_state_8bits_2__8[4]), ._3(tri_state_8bits_2__8[3]), ._2(tri_state_8bits_2__8[2]),
    ._1(tri_state_8bits_2__8[1]), ._0(tri_state_8bits_2__8[0]), .E(not_2_out), ._15(_103), ._14(_102),
    ._13(_101), ._12(_100), ._11(_99), ._10(_98), ._9(_97), ._8(_96));
  Control_Module control_module_1 (
    .US0(control_module_1_us0), .US1(control_module_1_us1), .US2(control_module_1_us2),
    .PBS0(control_module_1_pbs0), .PBS1(control_module_1_pbs1), .Sel_SP(control_module_1_sel_sp),
    .ULA_Bus(control_module_1_ula_bus), .BUF_Clock(control_module_1_buf_clock),
    .AC_Bus(control_module_1_ac_bus), .AC_Clock(control_module_1_ac_clock),
    .Reg_Bus(control_module_1_reg_bus), .Reg_Clock(control_module_1_reg_clock), .RAM_rd(RAM_read),
    .RAM_wr(RAM_write), .RAM_cs(control_module_1_ram_cs), .IN_bus(control_module_1_in_bus),
    .OUT_clock(control_module_1_out_clock), .Clock(or_1_out), .ROM_rd(ROM_read), .ROM_cs(ROM_cs),
    .PCH_bus(control_module_1_pch_bus), .PCL_bus(control_module_1_pcl_bus),
    .SP_Clock(control_module_1_sp_clock), .PCH_Clock(control_module_1_pch_clock),
    .SelDataPC(control_module_1_seldatapc), .DIRClock(control_module_1_dirclock),
    .SPIncDec(control_module_1_spincdec), .PCL_Clock(control_module_1_pcl_clock), .Flag_Z(ula_8bits_1_fz),
    .Flag_C(ula_8bits_1_fc), ._7(tri_state_8bits_2__8[7]), ._6(tri_state_8bits_2__8[6]),
    ._5(tri_state_8bits_2__8[5]), ._4(tri_state_8bits_2__8[4]), ._3(tri_state_8bits_2__8[3]),
    ._2(tri_state_8bits_2__8[2]), ._1(tri_state_8bits_2__8[1]), ._0(tri_state_8bits_2__8[0]), .R(Reset),
    .\Fim_de_Instrução (_104));  // open: SP_Enable
  Tri_State_8bits tri_state_8bits_2 (
    ._7(_23), ._6(_22), ._5(_21), ._4(_20), ._3(_19), ._2(_18), ._1(_17), ._0(_16), .E(or_2_out),
    ._15(tri_state_8bits_2__8[7]), ._14(tri_state_8bits_2__8[6]), ._13(tri_state_8bits_2__8[5]),
    ._12(tri_state_8bits_2__8[4]), ._11(tri_state_8bits_2__8[3]), ._10(tri_state_8bits_2__8[2]),
    ._9(tri_state_8bits_2__8[1]), ._8(tri_state_8bits_2__8[0]));
  not not_3 (not_3_out, control_module_1_sel_sp);
  Tri_State_8bits tri_state_8bits_3 (
    ._7(DIR__15), ._6(DIR__14), ._5(DIR__13), ._4(DIR__12), ._3(DIR__11), ._2(DIR__10), ._1(DIR__9),
    ._0(DIR__8), .E(not_3_out), ._15(_95), ._14(_94), ._13(_93), ._12(_92), ._11(_91), ._10(_90), ._9(_89),
    ._8(_88));
  and and_2 (RAM_cs, not_3_out, control_module_1_ram_cs);
  Registrador_8_bits_S_Gatilho DIR (
    .R(Reset), .C(control_module_1_dirclock), ._7(tri_state_8bits_2__8[7]), ._6(tri_state_8bits_2__8[6]),
    ._5(tri_state_8bits_2__8[5]), ._4(tri_state_8bits_2__8[4]), ._3(tri_state_8bits_2__8[3]),
    ._2(tri_state_8bits_2__8[2]), ._1(tri_state_8bits_2__8[1]), ._0(tri_state_8bits_2__8[0]), ._15(DIR__15),
    ._14(DIR__14), ._13(DIR__13), ._12(DIR__12), ._11(DIR__11), ._10(DIR__10), ._9(DIR__9), ._8(DIR__8));
  Counter_______8bits SP (
    ._0(SP__0), ._1(SP__1), ._2(SP__2), ._3(SP__3), ._4(SP__4), ._5(SP__5), ._6(SP__6), ._7(SP__7),
    .in_1(control_module_1_spincdec), .reset(Reset), .clock(control_module_1_sp_clock),
    .enable(control_module_1_sel_sp));
  Tri_State_8bits tri_state_8bits_4 (
    ._7(SP__7), ._6(SP__6), ._5(SP__5), ._4(SP__4), ._3(SP__3), ._2(SP__2), ._1(SP__1), ._0(SP__0),
    .E(control_module_1_sel_sp), ._15(tri_state_8bits_4__8[7]), ._14(tri_state_8bits_4__8[6]),
    ._13(tri_state_8bits_4__8[5]), ._12(tri_state_8bits_4__8[4]), ._11(tri_state_8bits_4__8[3]),
    ._10(tri_state_8bits_4__8[2]), ._9(tri_state_8bits_4__8[1]), ._8(tri_state_8bits_4__8[0]));
  and and_3 (and_3_out, control_module_1_ram_cs, control_module_1_sel_sp);
  Banco_4Reg_8Bits banco_4reg_8bits_1 (
    .R(Reset), ._7(tri_state_8bits_2__8[7]), ._6(tri_state_8bits_2__8[6]), ._5(tri_state_8bits_2__8[5]),
    ._4(tri_state_8bits_2__8[4]), ._3(tri_state_8bits_2__8[3]), ._2(tri_state_8bits_2__8[2]),
    ._1(tri_state_8bits_2__8[1]), ._0(tri_state_8bits_2__8[0]), .S1(control_module_1_pbs1),
    .S0(control_module_1_pbs0), .C(control_module_1_reg_clock), .E(control_module_1_reg_bus),
    ._15(tri_state_8bits_2__8[7]), ._14(tri_state_8bits_2__8[6]), ._13(tri_state_8bits_2__8[5]),
    ._12(tri_state_8bits_2__8[4]), ._11(tri_state_8bits_2__8[3]), ._10(tri_state_8bits_2__8[2]),
    ._9(tri_state_8bits_2__8[1]), ._8(tri_state_8bits_2__8[0]));
  RAM #(.bus("asynch")) ram_1 (
    .addr(tri_state_8bits_4__8), .data(tri_state_8bits_2__8), .sel(and_3_out), .ld(RAM_read), .clr(Reset));
  ULA_8bits ula_8bits_1 (
    .S0(control_module_1_us0), .S1(control_module_1_us1), .S2(control_module_1_us2),
    .E(control_module_1_ula_bus), .FZ(ula_8bits_1_fz), .FC(ula_8bits_1_fc), ._7(Acumulador__23),
    ._6(Acumulador__22), ._5(Acumulador__21), ._4(Acumulador__20), ._3(Acumulador__19), ._2(Acumulador__18),
    ._1(Acumulador__17), ._0(Acumulador__16), ._15(Buffer__15), ._14(Buffer__14), ._13(Buffer__13),
    ._12(Buffer__12), ._11(Buffer__11), ._10(Buffer__10), ._9(Buffer__9), ._23(tri_state_8bits_2__8[7]),
    ._22(tri_state_8bits_2__8[6]), ._21(tri_state_8bits_2__8[5]), ._20(tri_state_8bits_2__8[4]),
    ._19(tri_state_8bits_2__8[3]), ._18(tri_state_8bits_2__8[2]), ._17(tri_state_8bits_2__8[1]),
    ._16(tri_state_8bits_2__8[0]), ._8(Buffer__8));
  M_Addresser_16bits m_addresser_16bits_1 (
    .S(control_module_1_seldatapc), .CL(control_module_1_pcl_clock), .CH(control_module_1_pch_clock),
    .R(Reset), .PCH_BUS(control_module_1_pch_bus), ._7(tri_state_8bits_2__8[7]),
    ._6(tri_state_8bits_2__8[6]), ._5(tri_state_8bits_2__8[5]), ._4(tri_state_8bits_2__8[4]),
    ._3(tri_state_8bits_2__8[3]), ._2(tri_state_8bits_2__8[2]), ._1(tri_state_8bits_2__8[1]),
    ._0(tri_state_8bits_2__8[0]), .PCL_BUS(control_module_1_pcl_bus), ._23(_15), ._22(_14), ._21(_13),
    ._20(_12), ._19(_11), ._18(_10), ._17(_9), ._16(_8), ._31(tri_state_8bits_2__8[7]),
    ._30(tri_state_8bits_2__8[6]), ._29(tri_state_8bits_2__8[5]), ._28(tri_state_8bits_2__8[4]),
    ._27(tri_state_8bits_2__8[3]), ._26(tri_state_8bits_2__8[2]), ._25(tri_state_8bits_2__8[1]),
    ._24(tri_state_8bits_2__8[0]), ._15(_7), ._14(_6), ._13(_5), ._12(_4), ._11(_3), ._10(_2), ._9(_1),
    ._8(_0));
  Registrador_8bits_c__buffer Acumulador (
    .E(control_module_1_ac_bus), .R(Reset), .C(control_module_1_ac_clock), ._7(tri_state_8bits_2__8[7]),
    ._6(tri_state_8bits_2__8[6]), ._5(tri_state_8bits_2__8[5]), ._4(tri_state_8bits_2__8[4]),
    ._3(tri_state_8bits_2__8[3]), ._2(tri_state_8bits_2__8[2]), ._1(tri_state_8bits_2__8[1]),
    ._0(tri_state_8bits_2__8[0]), ._23(Acumulador__23), ._22(Acumulador__22), ._21(Acumulador__21),
    ._20(Acumulador__20), ._19(Acumulador__19), ._18(Acumulador__18), ._17(Acumulador__17),
    ._16(Acumulador__16), ._15(tri_state_8bits_2__8[7]), ._14(tri_state_8bits_2__8[6]),
    ._13(tri_state_8bits_2__8[5]), ._12(tri_state_8bits_2__8[4]), ._11(tri_state_8bits_2__8[3]),
    ._10(tri_state_8bits_2__8[2]), ._9(tri_state_8bits_2__8[1]), ._8(tri_state_8bits_2__8[0]));
  Registrador_8_bits_S_Gatilho Buffer (
    .R(Reset), .C(control_module_1_buf_clock), ._7(tri_state_8bits_2__8[7]), ._6(tri_state_8bits_2__8[6]),
    ._5(tri_state_8bits_2__8[5]), ._4(tri_state_8bits_2__8[4]), ._3(tri_state_8bits_2__8[3]),
    ._2(tri_state_8bits_2__8[2]), ._1(tri_state_8bits_2__8[1]), ._0(tri_state_8bits_2__8[0]),
    ._15(Buffer__15), ._14(Buffer__14), ._13(Buffer__13), ._12(Buffer__12), ._11(Buffer__11),
    ._10(Buffer__10), ._9(Buffer__9), ._8(Buffer__8));
  \Banco_de_portas_Entrada_e_Saída  \banco_de_portas_entrada_e_saída_1  (
    ._7(tri_state_8bits_2__8[7]), ._6(tri_state_8bits_2__8[6]), ._5(tri_state_8bits_2__8[5]),
    ._4(tri_state_8bits_2__8[4]), ._3(tri_state_8bits_2__8[3]), ._2(tri_state_8bits_2__8[2]),
    ._1(tri_state_8bits_2__8[1]), ._0(tri_state_8bits_2__8[0]), .S2(control_module_1_pbs1),
    .S1(control_module_1_pbs0), .E(control_module_1_in_bus), .C(control_module_1_out_clock), .R(Reset),
    ._15(_39), ._14(_38), ._13(_37), ._12(_36), ._11(_35), ._10(_34), ._9(_33), ._8(_32), ._23(_55),
    ._22(_54), ._21(_53), ._20(_52), ._19(_51), ._18(_50), ._17(_49), ._16(_48), ._31(_71), ._30(_70),
    ._29(_69), ._28(_68), ._27(_67), ._26(_66), ._25(_65), ._24(_64), ._39_2(_87), ._38_2(_86), ._37_2(_85),
    ._36_2(_84), ._35_2(_83), ._34_2(_82), ._33_2(_81), ._32(_80), ._40(tri_state_8bits_2__8[7]),
    ._39(tri_state_8bits_2__8[6]), ._38(tri_state_8bits_2__8[5]), ._37(tri_state_8bits_2__8[4]),
    ._36(tri_state_8bits_2__8[3]), ._35(tri_state_8bits_2__8[2]), ._34(tri_state_8bits_2__8[1]),
    ._33(tri_state_8bits_2__8[0]), ._56(_47), ._55(_46), ._54(_45), ._53(_44), ._52(_43), ._51(_42),
    ._50(_41), ._49(_40), ._64(_63), ._63(_62), ._62(_61), ._61(_60), ._60(_59), ._59(_58), ._58(_57),
    ._57(_56), ._72(_79), ._71(_78), ._70(_77), ._69(_76), ._68(_75), ._67(_74), ._66(_73), ._65(_72),
    ._48(_31), ._47(_30), ._46(_29), ._45(_28), ._44(_27), ._43(_26), ._42(_25), ._41(_24));

  // Notes on the sheet:
  //   Clock
  //   Máquina ++
  //   Projeto original: Jonathan Manoel Borges
  //   Adaptação LogiSim: Jean Jung
  //   Orientação: Miguel Alexandre Wisintainer
  //   EOI
  //   7.. RAM Data Output  ..0
  //   7.. Input  ..0
  //   7.. Output  ..0
  //   Saída Endereço Memória RAM
  //   Stack
  //   16.. Output  ..8
  //   Saída Endereçamento de Memória de Programa
  //   7.. Output  ..0
  //   7.. I0  ..0
  //   7.. O0  ..0
  //   7.. I1  ..0
  //   7.. O1  ..0
  //   7.. I2  ..0
  //   7.. O2  ..0
  //   7.. I3  ..0
  //   7.. O3  ..0
endmodule
