// Logisim project PC.circ as structural Verilog: 1 circuit, main circuit PC M++
module PC_M (
  input  _7,
  input  _6,
  input  _5,
  input  _4,
  input  _3,
  input  _2,
  input  _1,
  input  _0,
  input  _7_2,
  input  _6_2,
  input  _5_2,
  input  _4_2,
  input  _3_2,
  input  _2_2,
  input  _1_2,
  input  _0_2,
  input  _7_3,
  input  _6_3,
  input  _5_3,
  input  _4_3,
  input  _3_3,
  input  _2_3,
  input  _1_3,
  input  _0_3,
  input  _0_4,
  input  _1_4,
  input  _2_4,
  input  _3_4,
  input  _4_4,
  input  _5_4,
  input  _6_4,
  input  _7_4,
  input  Reset
);

  wire clock_1_out, m_1__32, m_1__33, m_1__34, m_1__35, m_1__36, m_1__37, m_1__38, m_1__39, m_1__64, m_1__65,
       m_1__66, m_1__67, m_1__68, m_1__69, m_1__70, m_1__71, m_1__80, m_1__81, m_1__82, m_1__83, m_1__84,
       m_1__85, m_1__86, m_1__87, m_1__104, m_1_ram_cs, m_1_ram_read, m_1_rom_cs;
  wire [3:0] m_1__48, m_1__52;
  wire [7:0] m_1__88, m_1__96;
  wire [15:0] m_1__0;

  Hex_Digit_Display hex_digit_display_1 (.value(m_1__52));  // open: dp
  M m_1 (
    .ROM_cs(m_1_rom_cs), .RAM_read(m_1_ram_read), .RAM_cs(m_1_ram_cs), ._105(clock_1_out), ._104(m_1__104),
    ._23(m_1__96[7]), ._22(m_1__96[6]), ._21(m_1__96[5]), ._20(m_1__96[4]), ._19(m_1__96[3]),
    ._18(m_1__96[2]), ._17(m_1__96[1]), ._16(m_1__96[0]), .Reset(Reset), ._31(_7_4), ._30(_6_4), ._29(_5_4),
    ._28(_4_4), ._27(_3_4), ._26(_2_4), ._25(_1_4), ._24(_0_4), ._47(_7), ._46(_6), ._45(_5), ._44(_4),
    ._43(_3), ._42(_2), ._41(_1), ._40(_0), ._63(_7_2), ._62(_6_2), ._61(_5_2), ._60(_4_2), ._59(_3_2),
    ._58(_2_2), ._57(_1_2), ._56(_0_2), ._79(_7_3), ._78(_6_3), ._77(_5_3), ._76(_4_3), ._75(_3_3),
    ._74(_2_3), ._73(_1_3), ._72(_0_3), ._103(m_1__96[7]), ._102(m_1__96[6]), ._101(m_1__96[5]),
    ._100(m_1__96[4]), ._99(m_1__96[3]), ._98(m_1__96[2]), ._97(m_1__96[1]), ._96(m_1__96[0]),
    ._95(m_1__88[7]), ._94(m_1__88[6]), ._93(m_1__88[5]), ._92(m_1__88[4]), ._91(m_1__88[3]),
    ._90(m_1__88[2]), ._89(m_1__88[1]), ._88(m_1__88[0]), ._15(m_1__0[15]), ._14(m_1__0[14]),
    ._13(m_1__0[13]), ._12(m_1__0[12]), ._11(m_1__0[11]), ._10(m_1__0[10]), ._9(m_1__0[9]), ._8(m_1__0[8]),
    ._7(m_1__0[7]), ._6(m_1__0[6]), ._5(m_1__0[5]), ._4(m_1__0[4]), ._3(m_1__0[3]), ._2(m_1__0[2]),
    ._1(m_1__0[1]), ._0(m_1__0[0]), ._39(m_1__39), ._38(m_1__38), ._37(m_1__37), ._36(m_1__36),
    ._35(m_1__35), ._34(m_1__34), ._33(m_1__33), ._32(m_1__32), ._55(m_1__52[3]), ._54(m_1__52[2]),
    ._53(m_1__52[1]), ._52(m_1__52[0]), ._51(m_1__48[3]), ._50(m_1__48[2]), ._49(m_1__48[1]),
    ._48(m_1__48[0]), ._71(m_1__71), ._70(m_1__70), ._69(m_1__69), ._68(m_1__68), ._67(m_1__67),
    ._66(m_1__66), ._65(m_1__65), ._64(m_1__64), ._87(m_1__87), ._86(m_1__86), ._85(m_1__85), ._84(m_1__84),
    ._83(m_1__83), ._82(m_1__82), ._81(m_1__81), ._80(m_1__80));  // open: ROM_read, RAM_write
  LED u__0 (.in(m_1__32));
  LED u__1 (.in(m_1__33));
  LED u__2 (.in(m_1__34));
  LED u__3 (.in(m_1__35));
  LED u__4 (.in(m_1__36));
  LED u__5 (.in(m_1__37));
  LED u__6 (.in(m_1__38));
  LED u__7 (.in(m_1__39));
  Hex_Digit_Display hex_digit_display_2 (.value(m_1__48));  // open: dp
  LED u__7_2 (.in(m_1__71));
  LED u__5_2 (.in(m_1__69));
  LED u__3_2 (.in(m_1__67));
  LED u__6_2 (.in(m_1__70));
  LED u__4_2 (.in(m_1__68));
  LED u__1_2 (.in(m_1__65));
  LED u__2_2 (.in(m_1__66));
  LED u__0_2 (.in(m_1__64));
  LED u__7_3 (.in(m_1__87));
  LED u__6_3 (.in(m_1__86));
  LED u__4_3 (.in(m_1__84));
  LED u__3_3 (.in(m_1__83));
  LED u__5_3 (.in(m_1__85));
  Clock clock_1 (.out(clock_1_out));
  LED u__0_3 (.in(m_1__80));
  LED u__1_3 (.in(m_1__81));
  LED u__2_3 (.in(m_1__82));
  LED \Fim_de_Instrução  (.in(m_1__104));
  ROM #(.addrWidth(16)) rom_1 (.addr(m_1__0), .data(m_1__96), .sel(m_1_rom_cs));
  RAM #(.bus("asynch")) ram_1 (.addr(m_1__88), .data(m_1__96), .sel(m_1_ram_cs), .ld(m_1_ram_read), .clr(Reset));

  // Notes on the sheet:
  //   ROM
  //   RAM
  //   contents of rom_1 (hex, n*v repeats v):
  //   7 c0 a c3 7 3 0 4
endmodule
