// Logisim project PortBank.circ as structural Verilog: 1 circuit, main circuit Banco de portas Entrada e Saída
// Port Bank
module \Banco_de_portas_Entrada_e_Saída  (
  input  _48,
  input  _47,
  input  _46,
  input  _45,
  input  _44,
  input  _43,
  input  _42,
  input  _41,
  input  _56,
  input  _55,
  input  _54,
  input  _53,
  input  _52,
  input  _51,
  input  _50,
  input  _49,
  input  _64,
  input  _63,
  input  _62,
  input  _61,
  input  _60,
  input  _59,
  input  _58,
  input  _57,
  input  _72,
  input  _71,
  input  _70,
  input  _69,
  input  _68,
  input  _67,
  input  _66,
  input  _65,
  input  S2,
  input  S1,
  input  _7,
  input  _6,
  input  E,
  input  _5,
  input  _4,
  input  _3,
  input  _2,
  input  _1,
  input  _0,
  input  C,
  input  R,
  output _40,
  output _39,
  output _38,
  output _37,
  output _36,
  output _35,
  output _34,
  output _33,
  output _15,
  output _14,
  output _13,
  output _12,
  output _11,
  output _10,
  output _9,
  output _8,
  output _23,
  output _22,
  output _21,
  output _20,
  output _19,
  output _18,
  output _17,
  output _16,
  output _31,
  output _30,
  output _29,
  output _28,
  output _27,
  output _26,
  output _25,
  output _24,
  output _39_2,
  output _38_2,
  output _37_2,
  output _36_2,
  output _35_2,
  output _34_2,
  output _33_2,
  output _32
);

  wire demux4_1_out_4, demux4_1_out_5, demux4_1_out_6, demux4_1_out_7, demux4_2_out_4, demux4_2_out_5,
       demux4_2_out_6, demux4_2_out_7;

  Tri_State_8bits tri_state_8bits_1 (
    ._7(_48), ._6(_47), ._5(_46), ._4(_45), ._3(_44), ._2(_43), ._1(_42), ._0(_41), .E(demux4_1_out_7),
    ._15(_40), ._14(_39), ._13(_38), ._12(_37), ._11(_36), ._10(_35), ._9(_34), ._8(_33));
  Registrador_8bits R0 (
    .E(1'b1), .R(R), .C(demux4_2_out_7), ._7(_7), ._6(_6), ._5(_5), ._4(_4), ._3(_3), ._2(_2), ._1(_1),
    ._0(_0), ._15(_15), ._14(_14), ._13(_13), ._12(_12), ._11(_11), ._10(_10), ._9(_9), ._8(_8));
  Tri_State_8bits tri_state_8bits_2 (
    ._7(_56), ._6(_55), ._5(_54), ._4(_53), ._3(_52), ._2(_51), ._1(_50), ._0(_49), .E(demux4_1_out_6),
    ._15(_40), ._14(_39), ._13(_38), ._12(_37), ._11(_36), ._10(_35), ._9(_34), ._8(_33));
  Tri_State_8bits tri_state_8bits_3 (
    ._7(_64), ._6(_63), ._5(_62), ._4(_61), ._3(_60), ._2(_59), ._1(_58), ._0(_57), .E(demux4_1_out_5),
    ._15(_40), ._14(_39), ._13(_38), ._12(_37), ._11(_36), ._10(_35), ._9(_34), ._8(_33));
  Registrador_8bits R1 (
    .E(1'b1), .R(R), .C(demux4_2_out_6), ._7(_7), ._6(_6), ._5(_5), ._4(_4), ._3(_3), ._2(_2), ._1(_1),
    ._0(_0), ._15(_23), ._14(_22), ._13(_21), ._12(_20), ._11(_19), ._10(_18), ._9(_17), ._8(_16));
  Registrador_8bits R2 (
    .E(1'b1), .R(R), .C(demux4_2_out_5), ._7(_7), ._6(_6), ._5(_5), ._4(_4), ._3(_3), ._2(_2), ._1(_1),
    ._0(_0), ._15(_31), ._14(_30), ._13(_29), ._12(_28), ._11(_27), ._10(_26), ._9(_25), ._8(_24));
  Tri_State_8bits tri_state_8bits_4 (
    ._7(_72), ._6(_71), ._5(_70), ._4(_69), ._3(_68), ._2(_67), ._1(_66), ._0(_65), .E(demux4_1_out_4),
    ._15(_40), ._14(_39), ._13(_38), ._12(_37), ._11(_36), ._10(_35), ._9(_34), ._8(_33));
  Registrador_8bits R3 (
    .E(1'b1), .R(R), .C(demux4_2_out_4), ._7(_7), ._6(_6), ._5(_5), ._4(_4), ._3(_3), ._2(_2), ._1(_1),
    ._0(_0), ._15(_39_2), ._14(_38_2), ._13(_37_2), ._12(_36_2), ._11(_35_2), ._10(_34_2), ._9(_33_2),
    ._8(_32));
  Demux4 demux4_1 (
    .S2(S2), .S1(S1), .D(E), .out_4(demux4_1_out_4), .out_5(demux4_1_out_5), .out_6(demux4_1_out_6),
    .out_7(demux4_1_out_7));
  Demux4 demux4_2 (
    .S2(S2), .S1(S1), .D(C), .out_4(demux4_2_out_4), .out_5(demux4_2_out_5), .out_6(demux4_2_out_6),
    .out_7(demux4_2_out_7));

  // Notes on the sheet:
  //   Bus out
  //   Bus in
  //   Banco I/O
  //   Jean Jung
  //   7.. I0  ..0
  //   7.. O0  ..0
  //   7.. I1  ..0
  //   7.. O1  ..0
  //   7.. I2  ..0
  //   7.. O2  ..0
  //   7.. I3  ..0
  //   7.. O3  ..0
  //   Clock
  //   Reset
endmodule
