// Logisim project Registers.circ as structural Verilog: 4 circuits, main circuit Registrador 8bits
// Reg 8bits
module Registrador_8bits (
  input  _7,
  input  _6,
  input  _5,
  input  _4,
  input  _3,
  input  _2,
  input  _1,
  input  _0,
  input  R,
  input  C,
  input  E,
  output _15,
  output _14,
  output _13,
  output _12,
  output _11,
  output _10,
  output _9,
  output _8
);

  wire registrador_8_bits_s_gatilho_1__8, registrador_8_bits_s_gatilho_1__9,
       registrador_8_bits_s_gatilho_1__10, registrador_8_bits_s_gatilho_1__11,
       registrador_8_bits_s_gatilho_1__12, registrador_8_bits_s_gatilho_1__13,
       registrador_8_bits_s_gatilho_1__14, registrador_8_bits_s_gatilho_1__15;

  Tri_State_8bits tri_state_8bits_1 (
    ._7(registrador_8_bits_s_gatilho_1__15), ._6(registrador_8_bits_s_gatilho_1__14),
    ._5(registrador_8_bits_s_gatilho_1__13), ._4(registrador_8_bits_s_gatilho_1__12),
    ._3(registrador_8_bits_s_gatilho_1__11), ._2(registrador_8_bits_s_gatilho_1__10),
    ._1(registrador_8_bits_s_gatilho_1__9), ._0(registrador_8_bits_s_gatilho_1__8), .E(E), ._15(_15),
    ._14(_14), ._13(_13), ._12(_12), ._11(_11), ._10(_10), ._9(_9), ._8(_8));
  Registrador_8_bits_S_Gatilho registrador_8_bits_s_gatilho_1 (
    .R(R), .C(C), ._7(_7), ._6(_6), ._5(_5), ._4(_4), ._3(_3), ._2(_2), ._1(_1), ._0(_0),
    ._15(registrador_8_bits_s_gatilho_1__15), ._14(registrador_8_bits_s_gatilho_1__14),
    ._13(registrador_8_bits_s_gatilho_1__13), ._12(registrador_8_bits_s_gatilho_1__12),
    ._11(registrador_8_bits_s_gatilho_1__11), ._10(registrador_8_bits_s_gatilho_1__10),
    ._9(registrador_8_bits_s_gatilho_1__9), ._8(registrador_8_bits_s_gatilho_1__8));
  LED u__7 (.in(registrador_8_bits_s_gatilho_1__15));
  LED u__6 (.in(registrador_8_bits_s_gatilho_1__14));
  LED u__4 (.in(registrador_8_bits_s_gatilho_1__12));
  LED u__3 (.in(registrador_8_bits_s_gatilho_1__11));
  LED u__5 (.in(registrador_8_bits_s_gatilho_1__13));
  LED u__1 (.in(registrador_8_bits_s_gatilho_1__9));
  LED u__2 (.in(registrador_8_bits_s_gatilho_1__10));
  LED u__0 (.in(registrador_8_bits_s_gatilho_1__8));

  // Notes on the sheet:
  //   Jean Jung
  //   Registrador de 8 bits
  //   Enable
  //   7.. Input  ..0
  //   7.. Output  ..0
  //   Dados Atuais
  //   Reset
  //   Clock
endmodule

// Reg 8bits s\g
module Registrador_8_bits_S_Gatilho (
  input  _7,
  input  _6,
  input  _5,
  input  _4,
  input  _3,
  input  _2,
  input  _1,
  input  _0,
  input  R,
  input  C,
  output _15,
  output _14,
  output _13,
  output _12,
  output _11,
  output _10,
  output _9,
  output _8
);

  D_Flip_Flop u__7 (.clk(C), .D(_7), .Q(_15), .reset(R));  // open: Qn, preset, en
  D_Flip_Flop u__6 (.clk(C), .D(_6), .Q(_14), .reset(R));  // open: Qn, preset, en
  D_Flip_Flop u__5 (.clk(C), .D(_5), .Q(_13), .reset(R));  // open: Qn, preset, en
  D_Flip_Flop u__4 (.clk(C), .D(_4), .Q(_12), .reset(R));  // open: Qn, preset, en
  D_Flip_Flop u__3 (.clk(C), .D(_3), .Q(_11), .reset(R));  // open: Qn, preset, en
  D_Flip_Flop u__2 (.clk(C), .D(_2), .Q(_10), .reset(R));  // open: Qn, preset, en
  D_Flip_Flop u__1 (.clk(C), .D(_1), .Q(_9), .reset(R));  // open: Qn, preset, en
  D_Flip_Flop u__0 (.clk(C), .D(_0), .Q(_8), .reset(R));  // open: Qn, preset, en
  LED _4_2 (.in(_12));
  LED _7_2 (.in(_15));
  LED _5_2 (.in(_13));
  LED _6_2 (.in(_14));
  LED _3_2 (.in(_11));
  LED _1_2 (.in(_9));
  LED _2_2 (.in(_10));
  LED _0_2 (.in(_8));

  // Notes on the sheet:
  //   Jean Jung
  //   Registrador de 8 bits S\Gatilho
  //   7.. Input  ..0
  //   7.. Output  ..0
  //   Reset
  //   Clock
  //   Dados Atuais
endmodule

// Reg 8bits c\buffer
module Registrador_8bits_c__buffer (
  input  _7,
  input  _6,
  input  _5,
  input  _4,
  input  _3,
  input  _2,
  input  _1,
  input  _0,
  input  R,
  input  C,
  input  E,
  output _23,
  output _22,
  output _21,
  output _20,
  output _19,
  output _18,
  output _17,
  output _16,
  output _15,
  output _14,
  output _13,
  output _12,
  output _11,
  output _10,
  output _9,
  output _8
);

  Registrador_8_bits_S_Gatilho registrador_8_bits_s_gatilho_1 (
    .R(R), .C(C), ._7(_7), ._6(_6), ._5(_5), ._4(_4), ._3(_3), ._2(_2), ._1(_1), ._0(_0), ._15(_23),
    ._14(_22), ._13(_21), ._12(_20), ._11(_19), ._10(_18), ._9(_17), ._8(_16));
  Tri_State_8bits tri_state_8bits_1 (
    ._7(_23), ._6(_22), ._5(_21), ._4(_20), ._3(_19), ._2(_18), ._1(_17), ._0(_16), .E(E), ._15(_15),
    ._14(_14), ._13(_13), ._12(_12), ._11(_11), ._10(_10), ._9(_9), ._8(_8));

  // Notes on the sheet:
  //   Jean Jung
  //   Enable
  //   Registrador de 8 bits c\buffer
  //   7.. Input  ..0
  //   7.. Buffer  ..0
  //   Reset
  //   Clock
  //   7.. Output ..0
endmodule

module Banco_4Reg_8Bits (
  input  _7,
  input  _6,
  input  _5,
  input  _4,
  input  _3,
  input  _2,
  input  _1,
  input  _0,
  input  S1,
  input  S0,
  input  C,
  input  E,
  input  R,
  output _15,
  output _14,
  output _13,
  output _12,
  output _11,
  output _10,
  output _9,
  output _8
);

  wire demux4_1_out_4, demux4_1_out_5, demux4_1_out_6, demux4_1_out_7, demux4_2_out_4, demux4_2_out_5,
       demux4_2_out_6, demux4_2_out_7;

  Registrador_8bits B (
    .E(demux4_2_out_7), .R(R), .C(demux4_1_out_7), ._7(_7), ._6(_6), ._5(_5), ._4(_4), ._3(_3), ._2(_2),
    ._1(_1), ._0(_0), ._15(_15), ._14(_14), ._13(_13), ._12(_12), ._11(_11), ._10(_10), ._9(_9), ._8(_8));
  Registrador_8bits u_C (
    .E(demux4_2_out_6), .R(R), .C(demux4_1_out_6), ._7(_7), ._6(_6), ._5(_5), ._4(_4), ._3(_3), ._2(_2),
    ._1(_1), ._0(_0), ._15(_15), ._14(_14), ._13(_13), ._12(_12), ._11(_11), ._10(_10), ._9(_9), ._8(_8));
  Registrador_8bits D (
    .E(demux4_2_out_5), .R(R), .C(demux4_1_out_5), ._7(_7), ._6(_6), ._5(_5), ._4(_4), ._3(_3), ._2(_2),
    ._1(_1), ._0(_0), ._15(_15), ._14(_14), ._13(_13), ._12(_12), ._11(_11), ._10(_10), ._9(_9), ._8(_8));
  Registrador_8bits u_E (
    .E(demux4_2_out_4), .R(R), .C(demux4_1_out_4), ._7(_7), ._6(_6), ._5(_5), ._4(_4), ._3(_3), ._2(_2),
    ._1(_1), ._0(_0), ._15(_15), ._14(_14), ._13(_13), ._12(_12), ._11(_11), ._10(_10), ._9(_9), ._8(_8));
  Demux4 demux4_1 (
    .S2(S1), .S1(S0), .D(C), .out_4(demux4_1_out_4), .out_5(demux4_1_out_5), .out_6(demux4_1_out_6),
    .out_7(demux4_1_out_7));
  Demux4 demux4_2 (
    .S2(S1), .S1(S0), .D(E), .out_4(demux4_2_out_4), .out_5(demux4_2_out_5), .out_6(demux4_2_out_6),
    .out_7(demux4_2_out_7));

  // Notes on the sheet:
  //   Jean Jung
  //   Banco de Registradores
  //   7.. Input  ..0
  //   7.. Output  ..0
  //   Seleção
  //   Clock
  //   Enable
  //   Reset
endmodule
