// Logisim project TriStates.circ as structural Verilog: 1 circuit, main circuit Tri State 8bits
// Tri State
module Tri_State_8bits (
  input  _7,
  input  _6,
  input  _5,
  input  _4,
  input  _3,
  input  _2,
  input  _1,
  input  _0,
  input  E,
  output _15,
  output _14,
  output _13,
  output _12,
  output _11,
  output _10,
  output _9,
  output _8
);

  assign _14 = E ? _6 : 1'bz;  // Controlled_Buffer controlled_buffer_1
  assign _15 = E ? _7 : 1'bz;  // Controlled_Buffer controlled_buffer_2
  assign _12 = E ? _4 : 1'bz;  // Controlled_Buffer controlled_buffer_3
  assign _10 = E ? _2 : 1'bz;  // Controlled_Buffer controlled_buffer_4
  assign _11 = E ? _3 : 1'bz;  // Controlled_Buffer controlled_buffer_5
  assign _13 = E ? _5 : 1'bz;  // Controlled_Buffer controlled_buffer_6
  assign _9 = E ? _1 : 1'bz;  // Controlled_Buffer controlled_buffer_7
  assign _8 = E ? _0 : 1'bz;  // Controlled_Buffer controlled_buffer_8

  // Notes on the sheet:
  //   Jean Jung
  //   Tri State 8bits
  //   Enable
  //   7.. Input  ..0
  //   7.. Output  ..0
endmodule
