// Logisim project ULA.circ as structural Verilog: 1 circuit, main circuit ULA 8bits
// ULA
module ULA_8bits (
  input  _7,
  input  _6,
  input  _5,
  input  _4,
  input  _3,
  input  _2,
  input  _1,
  input  _0,
  input  _15,
  input  _14,
  input  _13,
  input  _12,
  input  _11,
  input  _10,
  input  _9,
  input  _8,
  input  S0,
  input  S1,
  input  S2,
  input  E,
  output FZ,
  output FC,
  output _23,
  output _22,
  output _21,
  output _20,
  output _19,
  output _18,
  output _17,
  output _16
);

  wire and_8bits_2op_1__16, and_8bits_2op_1__17, and_8bits_2op_1__18, and_8bits_2op_1__19,
       and_8bits_2op_1__20, and_8bits_2op_1__21, and_8bits_2op_1__22, and_8bits_2op_1__23, C_FZ_out, C_out,
       inc_8bits_1__8, inc_8bits_1__9, inc_8bits_1__10, inc_8bits_1__11, inc_8bits_1__12, inc_8bits_1__13,
       inc_8bits_1__14, inc_8bits_1__15, inc_8bits_1_c, not_1_out, not_2_out, not_3_out, not_4_out,
       not_5_out, not_6_out, not_7_out, not_8_out, not_8bits_1__8, not_8bits_1__9, not_8bits_1__10,
       not_8bits_1__11, not_8bits_1__12, not_8bits_1__13, not_8bits_1__14, not_8bits_1__15, not_9_out,
       not_10_out, not_11_out, not_12_out, O1_out, O2_out, O3_out, O4_out, O5_out, O6_out, O7_out, O8_out,
       or_1_out, or_8bits_2op_1__16, or_8bits_2op_1__17, or_8bits_2op_1__18, or_8bits_2op_1__19,
       or_8bits_2op_1__20, or_8bits_2op_1__21, or_8bits_2op_1__22, or_8bits_2op_1__23, soma_sub_8bits_1__16,
       soma_sub_8bits_1__17, soma_sub_8bits_1__18, soma_sub_8bits_1__19, soma_sub_8bits_1__20,
       soma_sub_8bits_1__21, soma_sub_8bits_1__22, soma_sub_8bits_1__23, soma_sub_8bits_1_cn_1,
       tri_state_8bits_1__8, tri_state_8bits_1__9, tri_state_8bits_1__10, tri_state_8bits_1__11,
       tri_state_8bits_1__12, tri_state_8bits_1__13, tri_state_8bits_1__14, tri_state_8bits_1__15,
       tri_state_8bits_2__8, tri_state_8bits_2__9, tri_state_8bits_2__10, tri_state_8bits_2__11,
       tri_state_8bits_2__12, tri_state_8bits_2__13, tri_state_8bits_2__14, tri_state_8bits_2__15,
       tri_state_8bits_3__8, tri_state_8bits_3__9, tri_state_8bits_3__10, tri_state_8bits_3__11,
       tri_state_8bits_3__12, tri_state_8bits_3__13, tri_state_8bits_3__14, tri_state_8bits_3__15,
       tri_state_8bits_5__8, tri_state_8bits_5__9, tri_state_8bits_5__10, tri_state_8bits_5__11,
       tri_state_8bits_5__12, tri_state_8bits_5__13, tri_state_8bits_5__14, tri_state_8bits_5__15,
       tri_state_8bits_7__8, tri_state_8bits_7__9, tri_state_8bits_7__10, tri_state_8bits_7__11,
       tri_state_8bits_7__12, tri_state_8bits_7__13, tri_state_8bits_7__14, tri_state_8bits_7__15,
       tri_state_8bits_8__8, tri_state_8bits_8__9, tri_state_8bits_8__10, tri_state_8bits_8__11,
       tri_state_8bits_8__12, tri_state_8bits_8__13, tri_state_8bits_8__14, tri_state_8bits_8__15,
       tri_state_8bits_10__8, tri_state_8bits_10__9, tri_state_8bits_10__10, tri_state_8bits_10__11,
       tri_state_8bits_10__12, tri_state_8bits_10__13, tri_state_8bits_10__14, tri_state_8bits_10__15,
       tri_state_8bits_11__8, tri_state_8bits_11__9, tri_state_8bits_11__10, tri_state_8bits_11__11,
       tri_state_8bits_11__12, tri_state_8bits_11__13, tri_state_8bits_11__14, tri_state_8bits_11__15,
       tri_state_8bits_13__8, tri_state_8bits_13__9, tri_state_8bits_13__10, tri_state_8bits_13__11,
       tri_state_8bits_13__12, tri_state_8bits_13__13, tri_state_8bits_13__14, tri_state_8bits_13__15,
       tri_state_8bits_14__8, tri_state_8bits_14__9, tri_state_8bits_14__10, tri_state_8bits_14__11,
       tri_state_8bits_14__12, tri_state_8bits_14__13, tri_state_8bits_14__14, tri_state_8bits_14__15,
       tri_state_8bits_17__8, tri_state_8bits_17__9, tri_state_8bits_17__10, tri_state_8bits_17__11,
       tri_state_8bits_17__12, tri_state_8bits_17__13, tri_state_8bits_17__14, tri_state_8bits_17__15,
       xor_8bits_2op_1__16, xor_8bits_2op_1__17, xor_8bits_2op_1__18, xor_8bits_2op_1__19,
       xor_8bits_2op_1__20, xor_8bits_2op_1__21, xor_8bits_2op_1__22, xor_8bits_2op_1__23;

  not not_1 (not_1_out, S0);
  not not_2 (not_2_out, S1);
  not not_3 (not_3_out, S2);
  not not_4 (not_4_out, S1);
  not not_5 (not_5_out, S2);
  not not_6 (not_6_out, S0);
  not not_7 (not_7_out, S2);
  not not_8 (not_8_out, S2);
  not not_9 (not_9_out, S0);
  not not_10 (not_10_out, S1);
  not not_11 (not_11_out, S1);
  not not_12 (not_12_out, S0);
  and O1 (O1_out, not_1_out, not_2_out, not_3_out);
  and O2 (O2_out, S0, not_4_out, not_5_out);
  and O3 (O3_out, not_6_out, S1, not_7_out);
  and O4 (O4_out, S0, S1, not_8_out);
  and O5 (O5_out, not_9_out, not_10_out, S2);
  and O6 (O6_out, S0, not_11_out, S2);
  and O7 (O7_out, not_12_out, S1, S2);
  and O8 (O8_out, S0, S1, S2);
  Tri_State_8bits tri_state_8bits_1 (
    ._7(_7), ._6(_6), ._5(_5), ._4(_4), ._3(_3), ._2(_2), ._1(_1), ._0(_0), .E(or_1_out),
    ._15(tri_state_8bits_1__15), ._14(tri_state_8bits_1__14), ._13(tri_state_8bits_1__13),
    ._12(tri_state_8bits_1__12), ._11(tri_state_8bits_1__11), ._10(tri_state_8bits_1__10),
    ._9(tri_state_8bits_1__9), ._8(tri_state_8bits_1__8));
  SOMA_SUB_8bits soma_sub_8bits_1 (
    .Cn_1(soma_sub_8bits_1_cn_1), .O(O2_out), ._7(tri_state_8bits_1__15), ._6(tri_state_8bits_1__14),
    ._5(tri_state_8bits_1__13), ._4(tri_state_8bits_1__12), ._3(tri_state_8bits_1__11),
    ._2(tri_state_8bits_1__10), ._1(tri_state_8bits_1__9), ._0(tri_state_8bits_1__8),
    ._15(tri_state_8bits_3__15), ._14(tri_state_8bits_3__14), ._13(tri_state_8bits_3__13),
    ._12(tri_state_8bits_3__12), ._11(tri_state_8bits_3__11), ._10(tri_state_8bits_3__10),
    ._9(tri_state_8bits_3__9), ._8(tri_state_8bits_3__8), ._23(soma_sub_8bits_1__23),
    ._22(soma_sub_8bits_1__22), ._21(soma_sub_8bits_1__21), ._20(soma_sub_8bits_1__20),
    ._19(soma_sub_8bits_1__19), ._18(soma_sub_8bits_1__18), ._17(soma_sub_8bits_1__17),
    ._16(soma_sub_8bits_1__16));
  or or_1 (or_1_out, O1_out, O2_out);
  Tri_State_8bits tri_state_8bits_2 (
    ._7(soma_sub_8bits_1__23), ._6(soma_sub_8bits_1__22), ._5(soma_sub_8bits_1__21),
    ._4(soma_sub_8bits_1__20), ._3(soma_sub_8bits_1__19), ._2(soma_sub_8bits_1__18),
    ._1(soma_sub_8bits_1__17), ._0(soma_sub_8bits_1__16), .E(or_1_out), ._15(tri_state_8bits_2__15),
    ._14(tri_state_8bits_2__14), ._13(tri_state_8bits_2__13), ._12(tri_state_8bits_2__12),
    ._11(tri_state_8bits_2__11), ._10(tri_state_8bits_2__10), ._9(tri_state_8bits_2__9),
    ._8(tri_state_8bits_2__8));
  assign C_out = or_1_out ? soma_sub_8bits_1_cn_1 : 1'bz;  // Controlled_Buffer C
  Tri_State_8bits tri_state_8bits_3 (
    ._7(_15), ._6(_14), ._5(_13), ._4(_12), ._3(_11), ._2(_10), ._1(_9), ._0(_8), .E(or_1_out),
    ._15(tri_state_8bits_3__15), ._14(tri_state_8bits_3__14), ._13(tri_state_8bits_3__13),
    ._12(tri_state_8bits_3__12), ._11(tri_state_8bits_3__11), ._10(tri_state_8bits_3__10),
    ._9(tri_state_8bits_3__9), ._8(tri_state_8bits_3__8));
  assign C_out = O8_out ? inc_8bits_1_c : 1'bz;  // Controlled_Buffer C_Inc
  D_Flip_Flop d_ff_1 (.clk(E), .D(C_FZ_out), .Q(FZ));  // open: Qn, preset, en, reset
  D_Flip_Flop d_ff_2 (.clk(E), .D(C_out), .Q(FC));  // open: Qn, preset, en, reset
  nor C_FZ (C_FZ_out, tri_state_8bits_2__8, tri_state_8bits_2__9, tri_state_8bits_2__10, tri_state_8bits_2__11, tri_state_8bits_2__12, tri_state_8bits_2__13, tri_state_8bits_2__14, tri_state_8bits_2__15);
  Tri_State_8bits tri_state_8bits_4 (
    ._7(tri_state_8bits_2__15), ._6(tri_state_8bits_2__14), ._5(tri_state_8bits_2__13),
    ._4(tri_state_8bits_2__12), ._3(tri_state_8bits_2__11), ._2(tri_state_8bits_2__10),
    ._1(tri_state_8bits_2__9), ._0(tri_state_8bits_2__8), .E(E), ._15(_23), ._14(_22), ._13(_21), ._12(_20),
    ._11(_19), ._10(_18), ._9(_17), ._8(_16));
  Tri_State_8bits tri_state_8bits_5 (
    ._7(_7), ._6(_6), ._5(_5), ._4(_4), ._3(_3), ._2(_2), ._1(_1), ._0(_0), .E(O3_out),
    ._15(tri_state_8bits_5__15), ._14(tri_state_8bits_5__14), ._13(tri_state_8bits_5__13),
    ._12(tri_state_8bits_5__12), ._11(tri_state_8bits_5__11), ._10(tri_state_8bits_5__10),
    ._9(tri_state_8bits_5__9), ._8(tri_state_8bits_5__8));
  And_8bits_2op and_8bits_2op_1 (
    ._7(tri_state_8bits_5__15), ._15(tri_state_8bits_7__15), ._6(tri_state_8bits_5__14),
    ._14(tri_state_8bits_7__14), ._5(tri_state_8bits_5__13), ._13(tri_state_8bits_7__13),
    ._4(tri_state_8bits_5__12), ._12(tri_state_8bits_7__12), ._3(tri_state_8bits_5__11),
    ._11(tri_state_8bits_7__11), ._2(tri_state_8bits_5__10), ._10(tri_state_8bits_7__10),
    ._1(tri_state_8bits_5__9), ._9(tri_state_8bits_7__9), ._0(tri_state_8bits_5__8),
    ._8(tri_state_8bits_7__8), ._23(and_8bits_2op_1__23), ._22(and_8bits_2op_1__22),
    ._21(and_8bits_2op_1__21), ._20(and_8bits_2op_1__20), ._19(and_8bits_2op_1__19),
    ._18(and_8bits_2op_1__18), ._17(and_8bits_2op_1__17), ._16(and_8bits_2op_1__16));
  Tri_State_8bits tri_state_8bits_6 (
    ._7(and_8bits_2op_1__23), ._6(and_8bits_2op_1__22), ._5(and_8bits_2op_1__21), ._4(and_8bits_2op_1__20),
    ._3(and_8bits_2op_1__19), ._2(and_8bits_2op_1__18), ._1(and_8bits_2op_1__17), ._0(and_8bits_2op_1__16),
    .E(O3_out), ._15(tri_state_8bits_2__15), ._14(tri_state_8bits_2__14), ._13(tri_state_8bits_2__13),
    ._12(tri_state_8bits_2__12), ._11(tri_state_8bits_2__11), ._10(tri_state_8bits_2__10),
    ._9(tri_state_8bits_2__9), ._8(tri_state_8bits_2__8));
  Tri_State_8bits tri_state_8bits_7 (
    ._7(_15), ._6(_14), ._5(_13), ._4(_12), ._3(_11), ._2(_10), ._1(_9), ._0(_8), .E(O3_out),
    ._15(tri_state_8bits_7__15), ._14(tri_state_8bits_7__14), ._13(tri_state_8bits_7__13),
    ._12(tri_state_8bits_7__12), ._11(tri_state_8bits_7__11), ._10(tri_state_8bits_7__10),
    ._9(tri_state_8bits_7__9), ._8(tri_state_8bits_7__8));
  Tri_State_8bits tri_state_8bits_8 (
    ._7(_7), ._6(_6), ._5(_5), ._4(_4), ._3(_3), ._2(_2), ._1(_1), ._0(_0), .E(O4_out),
    ._15(tri_state_8bits_8__15), ._14(tri_state_8bits_8__14), ._13(tri_state_8bits_8__13),
    ._12(tri_state_8bits_8__12), ._11(tri_state_8bits_8__11), ._10(tri_state_8bits_8__10),
    ._9(tri_state_8bits_8__9), ._8(tri_state_8bits_8__8));
  Or_8bits_2op or_8bits_2op_1 (
    ._7(tri_state_8bits_8__15), ._15(tri_state_8bits_10__15), ._6(tri_state_8bits_8__14),
    ._14(tri_state_8bits_10__14), ._5(tri_state_8bits_8__13), ._13(tri_state_8bits_10__13),
    ._4(tri_state_8bits_8__12), ._12(tri_state_8bits_10__12), ._3(tri_state_8bits_8__11),
    ._11(tri_state_8bits_10__11), ._2(tri_state_8bits_8__10), ._10(tri_state_8bits_10__10),
    ._1(tri_state_8bits_8__9), ._9(tri_state_8bits_10__9), ._0(tri_state_8bits_8__8),
    ._8(tri_state_8bits_10__8), ._23(or_8bits_2op_1__23), ._22(or_8bits_2op_1__22), ._21(or_8bits_2op_1__21),
    ._20(or_8bits_2op_1__20), ._19(or_8bits_2op_1__19), ._18(or_8bits_2op_1__18), ._17(or_8bits_2op_1__17),
    ._16(or_8bits_2op_1__16));
  Tri_State_8bits tri_state_8bits_9 (
    ._7(or_8bits_2op_1__23), ._6(or_8bits_2op_1__22), ._5(or_8bits_2op_1__21), ._4(or_8bits_2op_1__20),
    ._3(or_8bits_2op_1__19), ._2(or_8bits_2op_1__18), ._1(or_8bits_2op_1__17), ._0(or_8bits_2op_1__16),
    .E(O4_out), ._15(tri_state_8bits_2__15), ._14(tri_state_8bits_2__14), ._13(tri_state_8bits_2__13),
    ._12(tri_state_8bits_2__12), ._11(tri_state_8bits_2__11), ._10(tri_state_8bits_2__10),
    ._9(tri_state_8bits_2__9), ._8(tri_state_8bits_2__8));
  Tri_State_8bits tri_state_8bits_10 (
    ._7(_15), ._6(_14), ._5(_13), ._4(_12), ._3(_11), ._2(_10), ._1(_9), ._0(_8), .E(O4_out),
    ._15(tri_state_8bits_10__15), ._14(tri_state_8bits_10__14), ._13(tri_state_8bits_10__13),
    ._12(tri_state_8bits_10__12), ._11(tri_state_8bits_10__11), ._10(tri_state_8bits_10__10),
    ._9(tri_state_8bits_10__9), ._8(tri_state_8bits_10__8));
  Tri_State_8bits tri_state_8bits_11 (
    ._7(_7), ._6(_6), ._5(_5), ._4(_4), ._3(_3), ._2(_2), ._1(_1), ._0(_0), .E(O5_out),
    ._15(tri_state_8bits_11__15), ._14(tri_state_8bits_11__14), ._13(tri_state_8bits_11__13),
    ._12(tri_state_8bits_11__12), ._11(tri_state_8bits_11__11), ._10(tri_state_8bits_11__10),
    ._9(tri_state_8bits_11__9), ._8(tri_state_8bits_11__8));
  Xor_8bits_2op xor_8bits_2op_1 (
    ._7(tri_state_8bits_11__15), ._15(tri_state_8bits_13__15), ._6(tri_state_8bits_11__14),
    ._14(tri_state_8bits_13__14), ._5(tri_state_8bits_11__13), ._13(tri_state_8bits_13__13),
    ._4(tri_state_8bits_11__12), ._12(tri_state_8bits_13__12), ._3(tri_state_8bits_11__11),
    ._11(tri_state_8bits_13__11), ._2(tri_state_8bits_11__10), ._10(tri_state_8bits_13__10),
    ._1(tri_state_8bits_11__9), ._9(tri_state_8bits_13__9), ._0(tri_state_8bits_11__8),
    ._8(tri_state_8bits_13__8), ._23(xor_8bits_2op_1__23), ._22(xor_8bits_2op_1__22),
    ._21(xor_8bits_2op_1__21), ._20(xor_8bits_2op_1__20), ._19(xor_8bits_2op_1__19),
    ._18(xor_8bits_2op_1__18), ._17(xor_8bits_2op_1__17), ._16(xor_8bits_2op_1__16));
  Tri_State_8bits tri_state_8bits_12 (
    ._7(xor_8bits_2op_1__23), ._6(xor_8bits_2op_1__22), ._5(xor_8bits_2op_1__21), ._4(xor_8bits_2op_1__20),
    ._3(xor_8bits_2op_1__19), ._2(xor_8bits_2op_1__18), ._1(xor_8bits_2op_1__17), ._0(xor_8bits_2op_1__16),
    .E(O5_out), ._15(tri_state_8bits_2__15), ._14(tri_state_8bits_2__14), ._13(tri_state_8bits_2__13),
    ._12(tri_state_8bits_2__12), ._11(tri_state_8bits_2__11), ._10(tri_state_8bits_2__10),
    ._9(tri_state_8bits_2__9), ._8(tri_state_8bits_2__8));
  Tri_State_8bits tri_state_8bits_13 (
    ._7(_15), ._6(_14), ._5(_13), ._4(_12), ._3(_11), ._2(_10), ._1(_9), ._0(_8), .E(O5_out),
    ._15(tri_state_8bits_13__15), ._14(tri_state_8bits_13__14), ._13(tri_state_8bits_13__13),
    ._12(tri_state_8bits_13__12), ._11(tri_state_8bits_13__11), ._10(tri_state_8bits_13__10),
    ._9(tri_state_8bits_13__9), ._8(tri_state_8bits_13__8));
  Tri_State_8bits tri_state_8bits_14 (
    ._7(_15), ._6(_14), ._5(_13), ._4(_12), ._3(_11), ._2(_10), ._1(_9), ._0(_8), .E(O6_out),
    ._15(tri_state_8bits_14__15), ._14(tri_state_8bits_14__14), ._13(tri_state_8bits_14__13),
    ._12(tri_state_8bits_14__12), ._11(tri_state_8bits_14__11), ._10(tri_state_8bits_14__10),
    ._9(tri_state_8bits_14__9), ._8(tri_state_8bits_14__8));
  Not_8bits not_8bits_1 (
    ._7(tri_state_8bits_14__15), ._6(tri_state_8bits_14__14), ._5(tri_state_8bits_14__13),
    ._4(tri_state_8bits_14__12), ._3(tri_state_8bits_14__11), ._2(tri_state_8bits_14__10),
    ._1(tri_state_8bits_14__9), ._0(tri_state_8bits_14__8), ._15(not_8bits_1__15), ._14(not_8bits_1__14),
    ._13(not_8bits_1__13), ._12(not_8bits_1__12), ._11(not_8bits_1__11), ._10(not_8bits_1__10),
    ._9(not_8bits_1__9), ._8(not_8bits_1__8));
  Tri_State_8bits tri_state_8bits_15 (
    ._7(not_8bits_1__15), ._6(not_8bits_1__14), ._5(not_8bits_1__13), ._4(not_8bits_1__12),
    ._3(not_8bits_1__11), ._2(not_8bits_1__10), ._1(not_8bits_1__9), ._0(not_8bits_1__8), .E(O6_out),
    ._15(tri_state_8bits_2__15), ._14(tri_state_8bits_2__14), ._13(tri_state_8bits_2__13),
    ._12(tri_state_8bits_2__12), ._11(tri_state_8bits_2__11), ._10(tri_state_8bits_2__10),
    ._9(tri_state_8bits_2__9), ._8(tri_state_8bits_2__8));
  Tri_State_8bits tri_state_8bits_16 (
    ._7(_15), ._6(_14), ._5(_13), ._4(_12), ._3(_11), ._2(_10), ._1(_9), ._0(_8), .E(O7_out),
    ._15(tri_state_8bits_2__15), ._14(tri_state_8bits_2__14), ._13(tri_state_8bits_2__13),
    ._12(tri_state_8bits_2__12), ._11(tri_state_8bits_2__11), ._10(tri_state_8bits_2__10),
    ._9(tri_state_8bits_2__9), ._8(tri_state_8bits_2__8));
  Tri_State_8bits tri_state_8bits_17 (
    ._7(_15), ._6(_14), ._5(_13), ._4(_12), ._3(_11), ._2(_10), ._1(_9), ._0(_8), .E(O8_out),
    ._15(tri_state_8bits_17__15), ._14(tri_state_8bits_17__14), ._13(tri_state_8bits_17__13),
    ._12(tri_state_8bits_17__12), ._11(tri_state_8bits_17__11), ._10(tri_state_8bits_17__10),
    ._9(tri_state_8bits_17__9), ._8(tri_state_8bits_17__8));
  Inc_8bits inc_8bits_1 (
    .C(inc_8bits_1_c), ._7(tri_state_8bits_17__15), ._6(tri_state_8bits_17__14), ._5(tri_state_8bits_17__13),
    ._4(tri_state_8bits_17__12), ._3(tri_state_8bits_17__11), ._2(tri_state_8bits_17__10),
    ._1(tri_state_8bits_17__9), ._0(tri_state_8bits_17__8), ._15(inc_8bits_1__15), ._14(inc_8bits_1__14),
    ._13(inc_8bits_1__13), ._12(inc_8bits_1__12), ._11(inc_8bits_1__11), ._10(inc_8bits_1__10),
    ._9(inc_8bits_1__9), ._8(inc_8bits_1__8));
  Tri_State_8bits tri_state_8bits_18 (
    ._7(inc_8bits_1__15), ._6(inc_8bits_1__14), ._5(inc_8bits_1__13), ._4(inc_8bits_1__12),
    ._3(inc_8bits_1__11), ._2(inc_8bits_1__10), ._1(inc_8bits_1__9), ._0(inc_8bits_1__8), .E(O8_out),
    ._15(tri_state_8bits_2__15), ._14(tri_state_8bits_2__14), ._13(tri_state_8bits_2__13),
    ._12(tri_state_8bits_2__12), ._11(tri_state_8bits_2__11), ._10(tri_state_8bits_2__10),
    ._9(tri_state_8bits_2__9), ._8(tri_state_8bits_2__8));

  // Notes on the sheet:
  //   Jean Jung
  //   Select
  //   Enable
  //   ULA de 8 Operações c\ 8bits
  //   7.. Input A  ..0
  //   7.. Input B ..0
  //   7.. Output  ..0
endmodule
